// Logisim project CPU_testbench.circ as structural Verilog: 2 circuits, main circuit test
module test (
  output [31:0] out_1,
  output [31:0] out_2,
  output out_3,
  output [4:0] out_4,
  output [31:0] out_5,
  output out_6,
  output halt,
  output [31:0] out_8,
  output [31:0] out_9
);

  wire clock_1_out, comparator_1_gt;
  wire [15:0] counter_1_q;

  Clock clock_1 (.out(clock_1_out));
  Counter #(.width(16), .max('hfff), .ongoal("stay")) counter_1 (
    .Q(counter_1_q), .carry(halt), .clk(clock_1_out));  // open: load, D, count, clr
  Comparator #(.width(16), .mode("unsigned")) comparator_1 (
    .a(16'h1), .b(counter_1_q), .gt(comparator_1_gt));  // open: eq, lt
  module_main main_1 (
    .in_1(comparator_1_gt), .out_2(out_1), .out_3(out_2), .out_4(out_3), .out_5(out_4), .out_6(out_5),
    .out_7(out_6), .out_8(out_8), .out_9(out_9));
endmodule

module tb (
  input  in_1,
  output [31:0] out_2,
  output [31:0] out_3,
  output out_4,
  output [4:0] out_5,
  output [31:0] out_6,
  output out_7,
  output [31:0] out_8,
  output [31:0] out_9
);
endmodule
