// Logisim project Empty_CPU.circ as structural Verilog: 1 circuit, main circuit main
module main (
  input  in_1,
  output [31:0] out_2,
  output [31:0] out_3,
  output out_4,
  output [4:0] out_5,
  output [31:0] out_6,
  output out_7,
  output [31:0] out_8,
  output [31:0] out_9
);

  wire Clk;

  Clock clock_1 (.out(Clk));
  // Probe on out_2
  // Probe on out_3

  // Other names for the same wires on the sheet: DMWE = out_7; GRFWE = out_4; Instr[31:0] = out_2;
  //   MemAddr[31:0] = out_8; MemData[31:0] = out_9; PC[31:0] = out_3; RegAddr[4:0] = out_5; RegData[31:0] = out_6;
  //   Reset = in_1
endmodule
