// Logisim project CPU0.circ as structural Verilog: 19 circuits, main circuit main
module main (
  input  in_1,
  output [31:0] out_2,
  output [31:0] out_3,
  output out_4,
  output [4:0] out_5,
  output [31:0] out_6,
  output out_7,
  output [31:0] out_8,
  output [31:0] out_9
);

  wire alu_1_out_4, ALUSrc, Branch, clk, Jump, LUI, MemtoReg, ORI, PCSrc, RegDst, undriven, undriven_2;
  wire [2:0] ALUControl2_0;
  wire [31:0] datamem_1_out_6, HiImm, multiplexer_2_out, multiplexer_3_out, multiplexer_4_out, RD1, RORI,
       SignImm, ZeroImm;

  Clock clock_1 (.out(clk));
  IFU ifu_1 (.in_1(in_1), .in_2(clk), .in_3(PCSrc), .out_5(out_3), .out_6(out_2), .in_4(Jump));
  // Probe on out_3
  // Probe on out_2[31:26]
  // Probe on out_2
  controler controler_1 (
    .in_1(out_2[31:26]), .in_2(out_2[5:0]), .out_3(MemtoReg), .out_4(out_7), .\是否为Beq指令 (Branch),
    .out_6(ALUControl2_0), .out_7(ALUSrc), .out_8(RegDst), .out_9(out_4), .out_10(ORI), .out_11(LUI),
    .out_12(Jump));
  Multiplexer #(.width(5), .disabled(0)) multiplexer_1 (
    .in0(out_2[20:16]), .in1(out_2[15:11]), .out(out_5), .sel(RegDst));  // open: en
  // Probe on out_5
  // Probe on out_6
  // Probe on out_5
  // Probe on out_2[25:21]
  GRF grf_1 (
    .in_4(out_2[25:21]), .in_5(out_2[20:16]), .in_6(out_5), .in_7(out_6), .out_8(RD1), .out_9(out_9),
    .in_1(clk), .in_2(in_1), .in_3(out_4));
  // Probe on RD1
  assign ZeroImm = {{16{1'b0}}, out_2[15:0]};  // Bit_Extender bit_extender_1
  assign SignImm = {{16{out_2[15]}}, out_2[15:0]};  // Bit_Extender bit_extender_2
  Shifter #(.width(32)) shifter_1 (.in(SignImm), .\dist (5'b10000), .out(HiImm));
  assign RORI = ZeroImm | RD1;  // OR_Gate or_1, 32 bits wide
  // Probe on ALUControl2_0
  Multiplexer #(.width(32), .disabled(0)) multiplexer_2 (
    .in0(out_9), .in1(SignImm), .out(multiplexer_2_out), .sel(ALUSrc), .en(undriven));
  ALU alu_1 (.in_2(RD1), .in_3(multiplexer_2_out), .out_4(alu_1_out_4), .out_5(out_8), .in_1(ALUControl2_0));
  and and_1 (PCSrc, Branch, alu_1_out_4);
  DataMem datamem_1 (.in_3(out_8), .in_4(out_9), .out_6(datamem_1_out_6), .in_1(clk), .in_2(out_7), .in_5(in_1));
  Multiplexer #(.width(32)) multiplexer_3 (
    .in0(out_8), .in1(datamem_1_out_6), .out(multiplexer_3_out), .sel(MemtoReg), .en(undriven_2));
  Multiplexer #(.width(32), .disabled(0)) multiplexer_4 (
    .in0(multiplexer_3_out), .in1(RORI), .out(multiplexer_4_out), .sel(ORI));  // open: en
  // Probe on out_8
  Multiplexer #(.width(32), .disabled(0)) multiplexer_5 (
    .in0(multiplexer_4_out), .in1(HiImm), .out(out_6), .sel(LUI));  // open: en

  // Other names for the same wires on the sheet: Instr[31:0] = out_2; instr15_0[15:0] = out_2[15:0];
  //   instr5_0[5:0] = out_2[5:0]; instr15_11[4:0] = out_2[15:11]; instr20_16[4:0] = out_2[20:16];
  //   instr25_21[4:0] = out_2[25:21]; instr31_26[5:0] = out_2[31:26]; MemAddr[31:0] = out_8; MemWrite = out_7;
  //   pc[31:0] = out_3; MemData[31:0] = out_9; RD2[31:0] = out_9; RegAddr[4:0] = out_5; RegData[31:0] = out_6;
  //   RegWrite = out_4; reset = in_1
endmodule

module inst_rom (
  input  [31:0] in_1,
  output [31:0] out_2
);

  wire [11:0] bit_extender_1_out;
  wire [31:0] subtractor_1_out;

  Subtractor #(.width(32)) subtractor_1 (.a(in_1), .b(32'h3000), .out(subtractor_1_out));  // open: bin, bout
  Bit_Extender #(.in_width(32), .out_width(12), .\type ("sign")) bit_extender_1 (
    .in(subtractor_1_out), .out(bit_extender_1_out));
  ROM #(.addrWidth(12), .dataWidth(32)) rom_1 (.addr(bit_extender_1_out), .data(out_2));  // open: sel

  // Other names for the same wires on the sheet: Instr[31:0] = out_2; PC[31:0] = in_1

  // Notes on the sheet:
  //   contents of rom_1 (hex, n*v repeats v):
  //   0 8c061cb0 0 3c08e274 ac08169c 36b5b79a 12adfffe 0 0 ac151b30 1446020 34ed5d10 3c01085e 0 3442512e
  //   1056fff5 2014820 8c0f070c 28b1020 ac090c10 20e3822 10c6020 ac11241c 1d21820 3c0fe9ec ac1109f4
  //   8c032c24 ac022f00 2ae3822 3c05418e ac180a94 35a59e3b 344266f1 1053ffec 2060022 ac080334 ac071880 0
  //   3c1918d5 0 ac181f1c 3c0dabdc 8c0d18f4 3c181b5e 3400d0e2 100efff5 3209820 3c10036a 3400cf71 1012fff1
  //   ac021400 1cb7822 a9a822 0 365266fe 1248fff8 34a6175b 3c01cbab 35ad9657 11b4fff4 3c0cc3b6 3c1087a7
  //   2f2b822 1205020 ac1624b0 8c011528 3c0a6256 3718c546 1315ffbc 1c76820 0 8c182768 ac1725b4 3694c452
  //   1281ffd8 261b020 34e7492e 10e2ffd5 3c09d247 ac1523c4 36101ef2 1213ffb3 215b820 36b5ded8 12afffed 0
  //   1e18020 ac060434 8c0409ac 352208f6 35b7e4fc 474822 3c13c934 ac121da0 8c0b1a6c ac1221d8 ac1721a8
  //   12a6822 8c14251c 35292582 35ad5b75 11b7ff9b 35ef9b82 11f8ffa6 3491247e 0 3c0b445b 356b2bb2 1172ffa1
  //   0 3c14f85a 8c0a0738 24e8820 341536f5 2a08822 0 34426abe 1047ff8f e10022 3c0ea7bb 36288ed3 0 34421159
  //   1050ffa1 36355879 3c097905 3c12f26a 8c181dec 30f9822 356b15b5 1161ffd6 4c9022 3c0269a5 0 1793822
  //   3c0dee0b 1508022 0 3c0f0592 322022 1551020 0 e74022 ac0c1068 1198822 2ac1022 0 3739b7f2 132cffeb
  //   8c0512c4 3c0db3ab 3c19ef58 ac0e2bac 34e79662 10e3ffe4 ac042494 35efd0d9 352e6e7c 2b12822 ac0027fc
  //   ac0a1218 34e73043 10f0ffe3 346b2f45 358c82de 118dff68 3013020 165b020 0 34c624d9 0 3c054d2f 3421854a
  //   1020ff60 358e18df 359820 ac182514 3421f78a 1029ffcc 3694d5d9 128eff6e 8c0e1978 ac002c0c 8c0a27f8 0
  //   2a15020 ac181dc8 46a020 2d03822 0 0 452822 356806ee ac0e178c 676022 1988020 3a022 b76020 3c10f97b
  //   cf4022 1b43822 3c05021e 0 35ef713e 11f0ffc2 34e7faa1 10e4ff8a ac0c1dcc 8c0e17c0 3c06c394 117c022
  //   ac0125f4 250820 ac0d0200 0 3c114705 2eb0822 354ac8ca 1156ff7e 0 8c0b298c 3408bdd4 a3b822 34d0b3b7
  //   255a020 14fb822 2690020 0 ac06135c 2717822 0 8c1611f4 3676394f 3631a8d0 1227ffc3 34400163 1ee9022
  //   3c0efc6c 8c0716c4 3c0cf916 ac152ac0 34c6cfa3 10d3ff9f 34f76136 35087e4d 1110ff63 8c101df4 2421022
  //   8c0c1108 0 0 370661eb 35ceeaaa 11cbffb0 3348822 35ef3847 11f7ffda ac0f2694 ac020228 638820 3c112cad
  //   309c820 af6822 3576bfd0 2d02022 103b822 26e8020 0 ac002af0 350b2a03 34ec0bd8 8c0f0f2c 3631ae0b
  //   1221ffd6 ac070968 0 34e2191a 3c0df6af ac0a17ec 3c17dbea 36b5c437 12b0feeb 3c0e897f 0 3c09ee6c
  //   36b4e087 8c0003a0 3443c656 0 35ef0061 11f7ff63 3718a3fc 1306ffb1 0 8c162798 3c12f850 8c141c90
  //   1340820 35a8dc4b 3539b6a5 1b34820 3610e456 1212ff01 3560edea 0 3492a76e 36311c49 122cffa2 35cef497
  //   11c4fed8 2748822 1af0820 3c1660e9 36310c19 1224ff07 2872020 0 36525710 1256ffa9 8c1222b8 34a52ae1
  //   10aaff3d 353111ef 8c010d28 34d3581e ac0f1b20 366eeb1e af3820 ac0a09e8 3c126ce9 3718f53e 1310ff62
  //   3c0df4b1 1d0c820 2650022 1129020 0 35b8037f ac01074c 3c0163e7 0 ac0d0110 0 36316c96 122fffde
  //   ac180768 3421b7f1 1023ff8c 8c020f84 358c237c 1184feaf 34f90d57 364df24b ac061734 3c085ca9 ac0327c0
  //   3c039b1c 360dbca5 35ef9574 11f9ff80 ac18199c b84020 3c01e3fd 360c5d79 3c181076 356b98bb 1163ffee
  //   35088faf 1107ff77 3705467a 354dc359 ac0d1a94 3c09af94 8c100824 0 3c00ca81 35d3c7b8 229c820 110b022
  //   1e12822 2328820 34cf85bf 35efa29f 11f5fec2 8c0915f8 35ef1134 11eeff2b ac0d143c ac151a28 0 1196822
  //   ac081f34 16b1822 3042020 0 1d49820 358c49fd 1192ff50 8c0a04f4 2566020 ac192f88 3421c3bb 1032feff
  //   8c041360 3631c2a2 1224ff5e 1394822 8c142484 30ab020 3647617d 1900020 35eff948 11e0ff39 1f37820
  //   ac021a14 ac0202d0 8c0f0390 3c0df06d 24b6020 34c6c519 10c7ff76 ac102598 8c0a0bac 8c0b0c9c 3739f481
  //   1333ffab 0 2e6c022 35ceb38f 11d0ffa7 36d63c9d 12ceffde ac172e64 304c022 0 c51820 8c0e2258 0 ac18056c
  //   8c11064c 0 1b3c822 1ea3822 37284728 35d1fe6c 3739c654 132bfe4f 2f15820 909820 36d60b4a 12d8ffcb
  //   cb0820 3c0c4752 35299ee2 1132fe69 ac030344 3518f6ea 0 35cee7a2 11c7feb4 ac0c1828 8c0b2644 0 3234820
  //   0 322c022 9022 26c9822 354a1935 1141feb9 1458022 8c0703c8 36946e87 1290fe56 ac0d013c 8c160c48
  //   3c00c7e9 358f0b07 0 3643ab47 35296810 112efe60 ac0b03bc aeb020 35262523 0 6d1020 36316f76 1223ffbe
  //   3c13b97d 1658020 3c181338 ab9822 8c0b1ce4 3c121eea e59022 0 1f05020 3c0f643f 34b033e0 220c02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
endmodule

module GRF (
  input  in_1,
  input  in_2,
  input  in_3,
  input  [4:0] in_4,
  input  [4:0] in_5,
  input  [4:0] in_6,
  input  [31:0] in_7,
  output [31:0] out_8,
  output [31:0] out_9
);

  wire [31:0] in_R0, in_R1, in_R2, in_R3, in_R4, in_R5, in_R6, in_R7, in_R8, in_R9, in_R10, in_R11, in_R12,
       in_R13, in_R14, in_R15, in_R16, in_R17, in_R18, in_R19, in_R20, in_R21, in_R22, in_R23, in_R24,
       in_R25, in_R26, in_R27, in_R28, in_R29, in_R30, in_R31, out_R0, out_R1, out_R2, out_R3, out_R4,
       out_R5, out_R6, out_R7, out_R8, out_R9, out_R10, out_R11, out_R12, out_R13, out_R14, out_R15, out_R16,
       out_R17, out_R18, out_R19, out_R20, out_R21, out_R22, out_R23, out_R24, out_R25, out_R26, out_R27,
       out_R28, out_R29, out_R30, out_R31;

  // Probe on in_R1
  // Probe on out_R1
  // Probe on out_8
  Multiplexer #(.select(5), .width(32)) multiplexer_1 (
    .in0(out_R0), .in1(out_R1), .in2(out_R2), .in3(out_R3), .in4(out_R4), .in5(out_R5), .in6(out_R6),
    .in7(out_R7), .in8(out_R8), .in9(out_R9), .in10(out_R10), .in11(out_R11), .in12(out_R12), .in13(out_R13),
    .in14(out_R14), .in15(out_R15), .in16(out_R16), .in17(out_R17), .in18(out_R18), .in19(out_R19),
    .in20(out_R20), .in21(out_R21), .in22(out_R22), .in23(out_R23), .in24(out_R24), .in25(out_R25),
    .in26(out_R26), .in27(out_R27), .in28(out_R28), .in29(out_R29), .in30(out_R30), .in31(out_R31),
    .out(out_8), .sel(in_4));  // open: en
  // Probe on in_4
  Register #(.width(32)) register_1 (.Q(out_R0), .clk(in_1), .clr(in_2));  // open: D, en
  Register #(.width(32)) register_2 (.D(in_R8), .Q(out_R8), .clk(in_1), .clr(in_2));  // open: en
  Register #(.width(32)) register_3 (.D(in_R16), .Q(out_R16), .clk(in_1), .clr(in_2));  // open: en
  Register #(.width(32)) register_4 (.D(in_R24), .Q(out_R24), .clk(in_1), .clr(in_2));  // open: en
  Register #(.width(32)) register_5 (.D(in_R1), .Q(out_R1), .clk(in_1), .clr(in_2));  // open: en
  Register #(.width(32)) register_6 (.D(in_R9), .Q(out_R9), .clk(in_1), .clr(in_2));  // open: en
  Register #(.width(32)) register_7 (.D(in_R17), .Q(out_R17), .clk(in_1), .clr(in_2));  // open: en
  Register #(.width(32)) register_8 (.D(in_R25), .Q(out_R25), .clk(in_1), .clr(in_2));  // open: en
  Register #(.width(32)) register_9 (.D(in_R2), .Q(out_R2), .clk(in_1), .clr(in_2));  // open: en
  Register #(.width(32)) register_10 (.D(in_R10), .Q(out_R10), .clk(in_1), .clr(in_2));  // open: en
  Register #(.width(32)) register_11 (.D(in_R18), .Q(out_R18), .clk(in_1), .clr(in_2));  // open: en
  Register #(.width(32)) register_12 (.D(in_R26), .Q(out_R26), .clk(in_1), .clr(in_2));  // open: en
  Multiplexer #(.select(5), .width(32)) multiplexer_2 (
    .in0(out_R0), .in1(out_R1), .in2(out_R2), .in3(out_R3), .in4(out_R4), .in5(out_R5), .in6(out_R6),
    .in7(out_R7), .in8(out_R8), .in9(out_R9), .in10(out_R10), .in11(out_R11), .in12(out_R12), .in13(out_R13),
    .in14(out_R14), .in15(out_R15), .in16(out_R16), .in17(out_R17), .in18(out_R18), .in19(out_R19),
    .in20(out_R20), .in21(out_R21), .in22(out_R22), .in23(out_R23), .in24(out_R24), .in25(out_R25),
    .in26(out_R26), .in27(out_R27), .in28(out_R28), .in29(out_R29), .in30(out_R30), .in31(out_R31),
    .out(out_9), .sel(in_5));  // open: en
  Register #(.width(32)) register_13 (.D(in_R3), .Q(out_R3), .clk(in_1), .clr(in_2));  // open: en
  Register #(.width(32)) register_14 (.D(in_R11), .Q(out_R11), .clk(in_1), .clr(in_2));  // open: en
  Register #(.width(32)) register_15 (.D(in_R19), .Q(out_R19), .clk(in_1), .clr(in_2));  // open: en
  Register #(.width(32)) register_16 (.D(in_R27), .Q(out_R27), .clk(in_1), .clr(in_2));  // open: en
  Register #(.width(32)) register_17 (.D(in_R4), .Q(out_R4), .clk(in_1), .clr(in_2));  // open: en
  Register #(.width(32)) register_18 (.D(in_R12), .Q(out_R12), .clk(in_1), .clr(in_2));  // open: en
  Register #(.width(32)) register_19 (.D(in_R20), .Q(out_R20), .clk(in_1), .clr(in_2));  // open: en
  Register #(.width(32)) register_20 (.D(in_R28), .Q(out_R28), .clk(in_1), .clr(in_2));  // open: en
  // Probe on in_R3
  Register #(.width(32)) register_21 (.D(in_R5), .Q(out_R5), .clk(in_1), .clr(in_2));  // open: en
  Register #(.width(32)) register_22 (.D(in_R13), .Q(out_R13), .clk(in_1), .clr(in_2));  // open: en
  Register #(.width(32)) register_23 (.D(in_R21), .Q(out_R21), .clk(in_1), .clr(in_2));  // open: en
  Register #(.width(32)) register_24 (.D(in_R29), .Q(out_R29), .clk(in_1), .clr(in_2));  // open: en
  // Probe on in_7
  // Probe on in_R1
  Demultiplexer #(.select(5), .width(32), .tristate("true")) demultiplexer_1 (
    .out0(in_R0), .out1(in_R1), .out2(in_R2), .out3(in_R3), .out4(in_R4), .out5(in_R5), .out6(in_R6),
    .out7(in_R7), .out8(in_R8), .out9(in_R9), .out10(in_R10), .out11(in_R11), .out12(in_R12), .out13(in_R13),
    .out14(in_R14), .out15(in_R15), .out16(in_R16), .out17(in_R17), .out18(in_R18), .out19(in_R19),
    .out20(in_R20), .out21(in_R21), .out22(in_R22), .out23(in_R23), .out24(in_R24), .out25(in_R25),
    .out26(in_R26), .out27(in_R27), .out28(in_R28), .out29(in_R29), .out30(in_R30), .out31(in_R31),
    .in(in_7), .sel(in_6), .en(in_3));
  // Probe on in_6
  Register #(.width(32)) register_25 (.D(in_R6), .Q(out_R6), .clk(in_1), .clr(in_2));  // open: en
  Register #(.width(32)) register_26 (.D(in_R14), .Q(out_R14), .clk(in_1), .clr(in_2));  // open: en
  Register #(.width(32)) register_27 (.D(in_R22), .Q(out_R22), .clk(in_1), .clr(in_2));  // open: en
  Register #(.width(32)) register_28 (.D(in_R30), .Q(out_R30), .clk(in_1), .clr(in_2));  // open: en
  Register #(.width(32)) register_29 (.D(in_R7), .Q(out_R7), .clk(in_1), .clr(in_2));  // open: en
  Register #(.width(32)) register_30 (.D(in_R15), .Q(out_R15), .clk(in_1), .clr(in_2));  // open: en
  Register #(.width(32)) register_31 (.D(in_R23), .Q(out_R23), .clk(in_1), .clr(in_2));  // open: en
  Register #(.width(32)) register_32 (.D(in_R31), .Q(out_R31), .clk(in_1), .clr(in_2));  // open: en

  // Other names for the same wires on the sheet: A1[4:0] = in_4; A2[4:0] = in_5; A3[4:0] = in_6; clk = in_1;
  //   RD1[31:0] = out_8; RD2[31:0] = out_9; reset = in_2; WD[31:0] = in_7; WE = in_3
endmodule

module ALU (
  input  [2:0] in_1,
  input  [31:0] in_2,
  input  [31:0] in_3,
  output out_4,
  output [31:0] out_5
);

  wire Zero;
  wire [31:0] and_1_out, AsubB, bit_extender_1_out, multiplexer_1_out, not_1_out, or_1_out;

  // Probe on in_3
  assign not_1_out = ~in_3;  // NOT_Gate not_1, 32 bits wide
  Multiplexer #(.width(32)) multiplexer_1 (
    .in0(in_3), .in1(not_1_out), .out(multiplexer_1_out), .sel(in_1[2]));  // open: en
  assign and_1_out = multiplexer_1_out & in_2;  // AND_Gate and_1, 32 bits wide
  assign or_1_out = multiplexer_1_out | in_2;  // OR_Gate or_1, 32 bits wide
  Adder #(.width(32)) adder_1 (.a(multiplexer_1_out), .b(in_2), .out(AsubB), .cin(in_1[2]));  // open: cout
  or or_2 (Zero, out_5[0], out_5[1], out_5[2], out_5[3], out_5[4], out_5[5], out_5[6], out_5[7], out_5[8], out_5[9], out_5[10], out_5[11], out_5[12], out_5[13], out_5[14], out_5[15], out_5[17], out_5[18], out_5[19], out_5[20], out_5[21], out_5[22], out_5[23], out_5[24], out_5[25], out_5[26], out_5[27], out_5[28], out_5[29], out_5[30], out_5[31], out_5[16]);
  Multiplexer #(.select(2), .width(32), .disabled(0)) multiplexer_2 (
    .in0(and_1_out), .in1(or_1_out), .in2(AsubB), .in3(bit_extender_1_out), .out(out_5), .sel(in_1[1:0]));  // open: en
  assign bit_extender_1_out = {{31{1'b0}}, AsubB[31]};  // Bit_Extender bit_extender_1
  // Probe on in_2
  // Probe on in_1[1:0]
  not not_2 (out_4, Zero);

  // Other names for the same wires on the sheet: ALUControl[2:0] = in_1; ALUControl2 = in_1[2];
  //   ALUControl1_0[1:0] = in_1[1:0]; SrcA[31:0] = in_2; SrcB[31:0] = in_3; Y[31:0] = out_5
endmodule

module DataMem (
  input  in_1,
  input  in_2,
  input  [31:0] in_3,
  input  [31:0] in_4,
  input  in_5,
  output [31:0] out_6
);

  wire not_1_out;
  wire [23:0] bit_extender_1_out;
  wire [31:0] shifter_1_out;

  // Probe on in_3
  Shifter #(.width(32), .shift("lr")) shifter_1 (.in(in_3), .\dist (5'b00010), .out(shifter_1_out));
  Bit_Extender #(.in_width(32), .out_width(24)) bit_extender_1 (.in(shifter_1_out), .out(bit_extender_1_out));
  // Probe on out_6
  not not_1 (not_1_out, in_2);
  RAM #(.addrWidth(24), .dataWidth(32), .bus("separate")) ram_1 (
    .addr(bit_extender_1_out), .din(in_4), .data(out_6), .str(in_2), .clk(in_1), .ld(not_1_out), .clr(in_5));  // open: sel

  // Other names for the same wires on the sheet: A[31:0] = in_3; clk = in_1; RD[31:0] = out_6; reset = in_5;
  //   WD[31:0] = in_4; WE = in_2
endmodule

module controler (
  input  [5:0] in_1,
  input  [5:0] in_2,
  output out_3,
  output out_4,
  output \是否为Beq指令 ,
  output [2:0] out_6,
  output out_7,
  output out_8,
  output out_9,
  output out_10,
  output out_11,
  output out_12
);

  wire [1:0] ALUOp1_0;

  MainTranslater maintranslater_1 (
    .in_1(in_1), .out_2(out_3), .out_3(out_4), .out_4(\是否为Beq指令 ), .out_5(out_7), .out_6(out_8),
    .out_7(out_9), .out_11(ALUOp1_0), .out_8(out_10), .out_9(out_11), .out_10(out_12));
  ALUTranslater alutranslater_1 (.in_2(in_2), .out_3(out_6), .in_1(ALUOp1_0));
  // Probe on out_6

  // Other names for the same wires on the sheet: ALUControl2_0[2:0] = out_6; ALUSrc = out_7; Branch = \是否为Beq指令 ;
  //   instr5_0[5:0] = in_2; instr31_26[5:0] = in_1; Jump = out_12; LUI = out_11; MemtoReg = out_3; MemWrite = out_4;
  //   ORI = out_10; RegDst = out_8; RegWrite = out_9

  // Notes on the sheet:
  //   当MemWrite为1时，写入存储器，为0时读取存储器
  //   是则为1
  //   控制进行什么ALU操作
  //   当MemtoReg为0时，将ALUResult存入寄存器；为1时，将ReadData存入寄存器
  //   ALUSrc为0时，执行R类指令，ALUSrc为1时，执行lw或sw指令
  //   当RegWrite为1时，写入寄存器文件，为0时读取寄存器文件
  //   RegWrite为1时，20：16为寄存器文件写入地址，RegWrite为0时，15：11为寄存器文件写入地址
endmodule

module MainTranslater (
  input  [5:0] in_1,
  output out_2,
  output out_3,
  output out_4,
  output out_5,
  output out_6,
  output out_7,
  output out_8,
  output out_9,
  output out_10,
  output [1:0] out_11
);

  wire andlogic_1_out_2, andlogic_1_out_3, andlogic_1_out_4, andlogic_1_out_5, andlogic_1_out_6,
       andlogic_1_out_7, andlogic_1_out_8;

  ANDLogic andlogic_1 (
    .in_1(in_1), .out_2(andlogic_1_out_2), .out_3(andlogic_1_out_3), .out_4(andlogic_1_out_4),
    .out_5(andlogic_1_out_5), .out_6(andlogic_1_out_6), .out_7(andlogic_1_out_7), .out_8(andlogic_1_out_8));
  ORLogic orlogic_1 (
    .R(andlogic_1_out_2), .ori(andlogic_1_out_3), .lw(andlogic_1_out_4), .sw(andlogic_1_out_5),
    .beq(andlogic_1_out_6), .lui(andlogic_1_out_7), .jump(andlogic_1_out_8), .out_14(out_11), .out_8(out_2),
    .out_9(out_3), .out_10(out_4), .out_11(out_5), .out_12(out_6), .out_13(out_7), .out_15(out_8),
    .out_16(out_9), .out_17(out_10));
  // Probe on out_11

  // Other names for the same wires on the sheet: ALUOp1_0[1:0] = out_11; ALUSrc = out_5; Branch = out_4;
  //   Jump = out_10; LUI = out_9; MemtoReg = out_2; MemWrite = out_3; Opcode[5:0] = in_1; ORI = out_8; RegDst = out_6;
  //   RegWrite = out_7

  // Notes on the sheet:
  //   ORLogic
endmodule

module ALUTranslater (
  input  [1:0] in_1,
  input  [5:0] in_2,
  output [2:0] out_3
);

  wire add_2_out, add_out, and_out, not_1_out, not_2_out, not_3_out, not_4_out, not_5_out, not_6_out,
       not_7_out, not_8_out, or_out, slt_out, sub_2_out, sub_out;

  not not_1 (not_1_out, in_1[1]);
  not not_2 (not_2_out, in_1[0]);
  not not_3 (not_3_out, in_2[4]);
  not not_4 (not_4_out, in_2[5]);
  not not_5 (not_5_out, in_2[3]);
  not not_6 (not_6_out, in_2[2]);
  not not_7 (not_7_out, in_2[1]);
  not not_8 (not_8_out, in_2[0]);
  and add (add_out, not_1_out, not_2_out);
  buf sub (sub_out, in_1[0]);  // AND_Gate
  and add_2 (add_2_out, in_1[1], in_2[5], not_3_out, not_5_out, not_6_out, not_7_out, not_8_out);
  and sub_2 (sub_2_out, in_1[1], in_2[5], not_3_out, not_5_out, not_6_out, in_2[1], not_8_out);
  and \and  (and_out, in_1[1], in_2[5], not_3_out, not_5_out, in_2[2], not_7_out, not_8_out);
  and \or  (or_out, in_1[1], in_2[5], not_3_out, not_5_out, in_2[2], not_7_out, in_2[0]);
  and slt (slt_out, in_1[1], in_2[5], not_3_out, in_2[3], not_6_out, in_2[1], not_8_out);
  or or_2 (out_3[2], sub_out, sub_2_out, slt_out);
  or or_3 (out_3[1], add_out, sub_out, add_2_out, sub_2_out, slt_out);
  or or_4 (out_3[0], slt_out, or_out);

  // Other names for the same wires on the sheet: ALUControl[2:0] = out_3; ALUControl0 = out_3[0];
  //   ALUControl1 = out_3[1]; ALUControl2 = out_3[2]; ALUOp[1:0] = in_1; ALUOp0 = in_1[0]; ALUOp1 = in_1[1];
  //   funct[5:0] = in_2; op0 = in_2[0]; op1 = in_2[1]; op2 = in_2[2]; op3 = in_2[3]; op4 = in_2[4]; op5 = in_2[5]
endmodule

module ANDLogic (
  input  [5:0] in_1,
  output out_2,
  output out_3,
  output out_4,
  output out_5,
  output out_6,
  output out_7,
  output out_8
);

  wire not_1_out, not_2_out, not_3_out, not_4_out, not_5_out, not_6_out;

  not not_1 (not_1_out, in_1[5]);
  not not_2 (not_2_out, in_1[4]);
  not not_3 (not_3_out, in_1[3]);
  not not_4 (not_4_out, in_1[2]);
  not not_5 (not_5_out, in_1[0]);
  not not_6 (not_6_out, in_1[1]);
  and R (out_2, not_1_out, not_2_out, not_3_out, not_4_out, not_6_out, not_5_out);
  and ori (out_3, not_1_out, not_2_out, in_1[3], in_1[2], not_6_out, in_1[0]);
  and lw (out_4, in_1[5], not_2_out, not_3_out, not_4_out, in_1[1], in_1[0]);
  and sw (out_5, in_1[5], not_2_out, in_1[3], not_4_out, in_1[1], in_1[0]);
  and beq (out_6, not_1_out, not_2_out, not_3_out, in_1[2], not_6_out, not_5_out);
  and lui (out_7, not_1_out, not_2_out, in_1[3], in_1[2], in_1[1], in_1[0]);
  and jump (out_8, not_1_out, not_2_out, not_3_out, not_4_out, in_1[1], not_5_out);

  // Other names for the same wires on the sheet: instr31_26[5:0] = in_1; op0 = in_1[0]; op1 = in_1[1]; op2 = in_1[2];
  //   op3 = in_1[3]; op4 = in_1[4]; op5 = in_1[5]
endmodule

module ORLogic (
  input  R,
  input  ori,
  input  lw,
  input  sw,
  input  beq,
  input  lui,
  input  jump,
  output out_8,
  output out_9,
  output out_10,
  output out_11,
  output out_12,
  output out_13,
  output [1:0] out_14,
  output out_15,
  output out_16,
  output out_17
);

  or or_1 (out_13, lw, R, ori, lui);
  buf or_2 (out_12, R);  // OR_Gate
  or or_3 (out_11, lw, sw, lw);
  buf or_4 (out_10, beq);  // OR_Gate
  buf or_5 (out_9, sw);  // OR_Gate
  buf or_6 (out_8, lw);  // OR_Gate
  buf or_7 (out_14[1], R);  // OR_Gate
  buf or_8 (out_14[0], beq);  // OR_Gate
  buf or_9 (out_15, ori);  // OR_Gate
  buf or_10 (out_16, lui);  // OR_Gate
  buf or_11 (out_17, jump);  // OR_Gate

  // Other names for the same wires on the sheet: ALUOp0 = out_14[0]; ALUOp1_0[1:0] = out_14; ALUOp1 = out_14[1];
  //   ALUSrc = out_11; Branch = out_10; jump_t = out_17; LUI_t = out_16; MemtoReg = out_8; MemWrite = out_9;
  //   ORI_t = out_15; RegDst = out_12; RegWrite = out_13
endmodule

module ALUANDLogic (
  input  [1:0] in_1,
  input  [5:0] in_2,
  output out_3,
  output out_4,
  output out_5,
  output out_6,
  output out_7,
  output out_8
);

  wire not_1_out, not_2_out, not_3_out, not_4_out, not_5_out, not_6_out, not_7_out, not_8_out;

  not not_1 (not_1_out, in_1[1]);
  not not_2 (not_2_out, in_1[0]);
  not not_3 (not_3_out, in_2[5]);
  not not_4 (not_4_out, in_2[4]);
  not not_5 (not_5_out, in_2[2]);
  not not_6 (not_6_out, in_2[3]);
  not not_7 (not_7_out, in_2[1]);
  not not_8 (not_8_out, in_2[0]);
  and add (out_3, in_2[5], not_4_out, not_6_out, not_5_out, not_7_out, not_8_out);
  and sub (out_4, in_2[5], not_4_out, not_6_out, not_5_out, in_2[1], not_8_out);
  and \and  (out_5, in_2[5], not_4_out, not_6_out, in_2[2], not_7_out, not_8_out);
  and \or  (out_6, in_2[5], not_4_out, not_6_out, in_2[2], not_7_out, in_2[0]);
  and slt (out_7, in_2[5], not_4_out, in_2[3], not_5_out, in_2[1], not_8_out);
  and and_2 (out_8, not_3_out, not_4_out, in_2[3], in_2[2], in_2[1], in_2[0]);

  // Other names for the same wires on the sheet: ALUOp[1:0] = in_1; ALUOp0 = in_1[0]; ALUOp1 = in_1[1];
  //   funct[5:0] = in_2; op0 = in_2[0]; op1 = in_2[1]; op2 = in_2[2]; op3 = in_2[3]; op4 = in_2[4]; op5 = in_2[5]
endmodule

module ALUORLogic (
  input  add,
  input  sub,
  input  \and ,
  input  \or ,
  input  slt,
  input  in_6
);

  wire ALUControl0, ALUControl1, ALUControl2;

  // OR_Gate or_1 has open pins: out=ALUControl2
  // OR_Gate or_2 has open pins: out=ALUControl1
  // OR_Gate or_3 has open pins: out=ALUControl0
endmodule

module IFU (
  input  in_1,
  input  in_2,
  input  in_3,
  input  in_4,
  output [31:0] out_5,
  output [31:0] out_6
);

  wire [31:0] bit_extender_1_out, multiplexer_1_out, multiplexer_2_out, PC_q, PCBranch, PCPlus4,
       shifter_1_out, xor_1_out;

  Multiplexer #(.width(32)) multiplexer_1 (
    .in0(PCPlus4), .in1(PCBranch), .out(multiplexer_1_out), .sel(in_3));  // open: en
  assign xor_1_out = 32'h3000 ^ multiplexer_2_out;  // XOR_Gate xor_1, 32 bits wide
  Multiplexer #(.width(32)) multiplexer_2 (
    .in0(multiplexer_1_out), .in1({out_5[31:28], out_6[25:0], 2'b00}), .out(multiplexer_2_out), .sel(in_4));  // open: en
  Register #(.width(32)) PC (.D(xor_1_out), .Q(PC_q), .clk(in_2), .clr(in_1));  // open: en
  assign out_5 = 32'h3000 ^ PC_q;  // XOR_Gate xor_2, 32 bits wide
  IM im_1 (.in_1(out_5), .out_2(out_6));
  Adder #(.width(32)) adder_1 (.a(out_5), .b(32'h4), .out(PCPlus4));  // open: cin, cout
  assign bit_extender_1_out = {{16{out_6[15]}}, out_6[15:0]};  // Bit_Extender bit_extender_1
  Shifter #(.width(32)) shifter_1 (.in(bit_extender_1_out), .\dist (5'b00010), .out(shifter_1_out));
  Adder #(.width(32)) adder_2 (.a(shifter_1_out), .b(PCPlus4), .out(PCBranch));  // open: cin, cout

  // Other names for the same wires on the sheet: Instr[31:0] = out_6; instr5_0[5:0] = out_6[5:0];
  //   instr15_0[15:0] = out_6[15:0]; instr15_11[4:0] = out_6[15:11]; instr20_16[4:0] = out_6[20:16];
  //   instr25_21[4:0] = out_6[25:21]; pc[31:0] = out_5; clk = in_2; instr31_26[5:0] = out_6[31:26]; Jump = in_4;
  //   PCSrc = in_3; reset = in_1
endmodule

module IM (
  input  [31:0] in_1,
  output [31:0] out_2
);

  wire [11:0] bit_extender_1_out;
  wire [31:0] divider_1_out, subtractor_1_out;

  // Probe on in_1
  // Probe on subtractor_1_out
  Subtractor #(.width(32)) subtractor_1 (.a(in_1), .b(32'h3000), .out(subtractor_1_out));  // open: bin, bout
  Divider #(.width(32)) divider_1 (.a(subtractor_1_out), .b(32'h4), .out(divider_1_out));  // open: upper, rem
  Bit_Extender #(.in_width(32), .out_width(12), .\type ("sign")) bit_extender_1 (
    .in(divider_1_out), .out(bit_extender_1_out));
  // Probe on divider_1_out
  // Probe on bit_extender_1_out
  ROM #(.addrWidth(12), .dataWidth(32)) rom_1 (.addr(bit_extender_1_out), .data(out_2));  // open: sel
  // Probe on out_2

  // Other names for the same wires on the sheet: Instr[31:0] = out_2; PC[31:0] = in_1

  // Notes on the sheet:
  //   contents of rom_1 (hex, n*v repeats v):
  //   34000000 34210001 34420002 34630003 34840004 34a50005 34c60006 34e70007 35080008 35290009 354a000a
  //   356b000b 358c000c 35ad000d 35ce000e 35ef000f 36100010 36310011 36520012 36730013 36940014 36b50015
  //   36d60016 36f70017 37180018 37390019 375a001a 377b001b 379c001c 37bd001d 37de001e 37ff001f 34210001
  //   ac010004 ac010008 ac01000c ac010010 ac010014 ac010018 ac01001c ac010020 ac010024 ac010028 ac01002c
  //   ac010030 ac010034 ac010038 ac01003c ac010040 ac010044 ac010048 ac01004c ac010050 ac010054 ac010058
  //   ac01005c ac010060 ac010064 ac010068 ac01006c ac010070 ac010074 ac010078 ac01007c 34210001 ac010000
  //   8c020000 8c030000 8c040000 8c050000 8c060000 8c070000 8c080000 8c090000 8c0a0000 8c0b0000 8c0c0000
  //   8c0d0000 8c0e0000 8c0f0000 8c100000 8c110000 8c120000 8c130000 8c140000 8c150000 8c160000 8c170000
  //   8c180000 8c190000 8c1a0000 8c1b0000 8c1c0000 8c1d0000 8c1e0000 8c1f0000 3421038b ac000000 8c010000
  //   ac010004 8c020004 ac020008 8c030008 ac03000c 8c04000c ac040010 8c050010 ac050014 8c060014 ac060018
  //   8c070018 ac07001c 8c08001c ac080020 8c090020 ac090024 8c0a0024 ac0a0028 8c0b0028 ac0b002c 8c0c002c
  //   ac0c0030 8c0d0030 ac0d0034 8c0e0034 ac0e0038 8c0f0038 ac0f003c 8c10003c ac100040 8c110040 ac110044
  //   8c120044 ac120048 8c130048 ac13004c 8c14004c ac140050 8c150050 ac150054 8c160054 ac160058 8c170058
  //   ac17005c 8c18005c ac180060 8c190060 ac190064 8c1a0064 ac1a0068 8c1b0068 ac1b006c 8c1c006c ac1c0070
  //   8c1d0070 ac1d0074 8c1e0074 ac1e0078 8c1f0078 ac1f007c 3c0100ea 3c0200ea 3c0300ea 3c0400ea 3c0500ea
  //   3c0600ea 3c0700ea 3c0800ea 3c0900ea 3c0a00ea 3c0b00ea 3c0c00ea 3c0d00ea 3c0e00ea 3c0f00ea c000cc1
  //   3c0100de 2018023 2218823 2419023 2619823 281a023 2a1a823 2c1b023 2e1b823 301c023 321c823 341d023
  //   361d823 381e023 3a1e823 3c1f023 c000cd1 2018021 2228821 2439021 2649821 285a021 2a6a821 2c7b021
  //   2e8b821 309c021 32ac821 34bd021 36cd821 38de021 3aee821 3cff021 3e00008 34010001 34020002 10220001
  //   210821 340c0001 340d0001 118d0001 421021 c000cdd c000ce2 c63021 c000ce2 1f7821 34050004 3e5f821
  //   1e00008 210821
endmodule

module \少用tunnel  (
  input  in_1,
  output [31:0] out_2,
  output [31:0] out_3,
  output out_4,
  output [4:0] out_5,
  output [31:0] out_6,
  output out_7,
  output [31:0] out_8,
  output [31:0] out_9
);

  wire ALUSrc, Branch, clock_1_out, LUI, MemtoReg, ORI, RegDst;
  wire [2:0] ALUControl2_0;
  wire [4:0] instr20_16, instr25_21, multiplexer_1_out;
  wire [5:0] instr5_0, instr31_26;
  wire [15:6] instr15_0;

  Clock clock_1 (.out(clock_1_out));
  IFU ifu_1 (
    .in_1(in_1), .in_2(clock_1_out), .out_6({instr31_26, instr25_21, instr20_16, instr15_0, instr5_0}));  // open: in_3, out_5, in_4
  controler controler_1 (
    .in_1(instr31_26), .in_2(instr5_0), .out_3(MemtoReg), .out_4(out_7), .\是否为Beq指令 (Branch),
    .out_6(ALUControl2_0), .out_7(ALUSrc), .out_8(RegDst), .out_9(out_4), .out_10(ORI), .out_11(LUI));  // open: out_12
  GRF grf_1 (
    .in_4(instr25_21), .in_5(instr20_16), .in_6(multiplexer_1_out));  // open: in_7, out_8, out_9, in_1, in_2, in_3
  Multiplexer #(.width(5)) multiplexer_1 (
    .in0(instr20_16), .in1(instr15_0[15:11]), .out(multiplexer_1_out), .sel(RegDst));  // open: en

  // Other names for the same wires on the sheet: instr[31:0] = out_2; instr15_0[5:0] = instr5_0;
  //   instr15_11[4:0] = instr15_0[15:11]; MemAddr[31:0] = out_8; MemData[31:0] = out_9; MemWrite = out_7;
  //   pc[31:0] = out_3; RegAddr[4:0] = out_5; RegData[31:0] = out_6; RegWrite = out_4; reset = in_1
endmodule

module \补码器  (
  input  [31:0] in_1,
  output [31:0] out_2
);

  wire [31:0] adder_1_out, negator_1_out;

  Negator #(.width(32)) negator_1 (.in(in_1), .out(negator_1_out));
  Adder #(.width(32)) adder_1 (.a(negator_1_out), .b(32'h1), .out(adder_1_out));  // open: cin, cout
  Multiplexer #(.width(32)) multiplexer_1 (.in0(in_1), .in1(adder_1_out), .out(out_2), .sel(in_1[31]));  // open: en

  // Other names for the same wires on the sheet: sign = in_1[31]
endmodule

module test (
  input  in_1
);

  wire main_1_out_4, main_1_out_7;
  wire [4:0] main_1_out_5;
  wire [31:0] main_1_out_2, main_1_out_3, main_1_out_6, main_1_out_8, main_1_out_9;

  main main_1 (
    .in_1(in_1), .out_2(main_1_out_2), .out_3(main_1_out_3), .out_4(main_1_out_4), .out_5(main_1_out_5),
    .out_6(main_1_out_6), .out_7(main_1_out_7), .out_8(main_1_out_8), .out_9(main_1_out_9));
endmodule

module copy (
  input  in_1,
  output [31:0] out_2,
  output [31:0] out_3,
  output out_4,
  output [4:0] out_5,
  output [31:0] out_6,
  output out_7,
  output [31:0] out_8,
  output [31:0] out_9
);

  wire alu_1_out_4, ALUSrc, Branch, clk, Jump, LUI, MemtoReg, ORI, PCSrc, RegDst, undriven, undriven_2;
  wire [2:0] ALUControl2_0;
  wire [31:0] datamem_1_out_6, HiImm, multiplexer_2_out, multiplexer_3_out, multiplexer_4_out, RD1, RORI,
       SignImm, ZeroImm;

  Clock clock_1 (.out(clk));
  IFU ifu_1 (.in_1(in_1), .in_2(clk), .in_3(PCSrc), .out_5(out_3), .out_6(out_2), .in_4(Jump));
  // Probe on out_3
  // Probe on out_2[31:26]
  // Probe on out_2
  controler controler_1 (
    .in_1(out_2[31:26]), .in_2(out_2[5:0]), .out_3(MemtoReg), .out_4(out_7), .\是否为Beq指令 (Branch),
    .out_6(ALUControl2_0), .out_7(ALUSrc), .out_8(RegDst), .out_9(out_4), .out_10(ORI), .out_11(LUI),
    .out_12(Jump));
  Multiplexer #(.width(5), .disabled(0)) multiplexer_1 (
    .in0(out_2[20:16]), .in1(out_2[15:11]), .out(out_5), .sel(RegDst));  // open: en
  // Probe on out_5
  // Probe on out_6
  // Probe on out_5
  // Probe on out_2[25:21]
  GRF grf_1 (
    .in_4(out_2[25:21]), .in_5(out_2[20:16]), .in_6(out_5), .in_7(out_6), .out_8(RD1), .out_9(out_9),
    .in_1(clk), .in_2(in_1), .in_3(out_4));
  // Probe on RD1
  assign ZeroImm = {{16{1'b0}}, out_2[15:0]};  // Bit_Extender bit_extender_1
  assign SignImm = {{16{out_2[15]}}, out_2[15:0]};  // Bit_Extender bit_extender_2
  Shifter #(.width(32)) shifter_1 (.in(SignImm), .\dist (5'b10000), .out(HiImm));
  assign RORI = ZeroImm | RD1;  // OR_Gate or_1, 32 bits wide
  // Probe on ALUControl2_0
  Multiplexer #(.width(32), .disabled(0)) multiplexer_2 (
    .in0(out_9), .in1(SignImm), .out(multiplexer_2_out), .sel(ALUSrc), .en(undriven));
  ALU alu_1 (.in_2(RD1), .in_3(multiplexer_2_out), .out_4(alu_1_out_4), .out_5(out_8), .in_1(ALUControl2_0));
  and and_1 (PCSrc, Branch, alu_1_out_4);
  DataMem datamem_1 (.in_3(out_8), .in_4(out_9), .out_6(datamem_1_out_6), .in_1(clk), .in_2(out_7), .in_5(in_1));
  Multiplexer #(.width(32)) multiplexer_3 (
    .in0(out_8), .in1(datamem_1_out_6), .out(multiplexer_3_out), .sel(MemtoReg), .en(undriven_2));
  Multiplexer #(.width(32), .disabled(0)) multiplexer_4 (
    .in0(multiplexer_3_out), .in1(RORI), .out(multiplexer_4_out), .sel(ORI));  // open: en
  // Probe on out_8
  Multiplexer #(.width(32), .disabled(0)) multiplexer_5 (
    .in0(multiplexer_4_out), .in1(HiImm), .out(out_6), .sel(LUI));  // open: en

  // Other names for the same wires on the sheet: Instr[31:0] = out_2; instr5_0[5:0] = out_2[5:0];
  //   instr15_0[15:0] = out_2[15:0]; instr15_11[4:0] = out_2[15:11]; instr20_16[4:0] = out_2[20:16];
  //   instr25_21[4:0] = out_2[25:21]; instr31_26[5:0] = out_2[31:26]; MemAddr[31:0] = out_8; MemWrite = out_7;
  //   pc[31:0] = out_3; MemData[31:0] = out_9; RD2[31:0] = out_9; RegAddr[4:0] = out_5; RegData[31:0] = out_6;
  //   RegWrite = out_4; reset = in_1
endmodule

module ext (
  input  [15:0] in_1
);

  wire [31:0] bit_extender_1_out;

  assign bit_extender_1_out = {{16{in_1[15]}}, in_1};  // Bit_Extender bit_extender_1
  // Probe on bit_extender_1_out
endmodule
