// Logisim project CPU0.circ as structural Verilog: 19 circuits, main circuit main
module main (
  input  in_1,
  output [31:0] out_2,
  output [31:0] out_3,
  output out_4,
  output [4:0] out_5,
  output [31:0] out_6,
  output out_7,
  output [31:0] out_8,
  output [31:0] out_9
);

  wire alu_1_out_4, ALUSrc, Branch, clk, Jump, LUI, MemtoReg, ORI, PCSrc, RegDst, undriven, undriven_2;
  wire [2:0] ALUControl2_0;
  wire [31:0] datamem_1_out_6, HiImm, multiplexer_2_out, multiplexer_3_out, multiplexer_4_out, RD1, RORI,
       SignImm, ZeroImm;

  Clock clock_1 (.out(clk));
  IFU ifu_1 (.in_1(in_1), .in_2(clk), .in_3(PCSrc), .out_5(out_3), .out_6(out_2), .in_4(Jump));
  // Probe on out_3
  // Probe on out_2[31:26]
  // Probe on out_2
  controler controler_1 (
    .in_1(out_2[31:26]), .in_2(out_2[5:0]), .out_3(MemtoReg), .out_4(out_7), .\是否为Beq指令 (Branch),
    .out_6(ALUControl2_0), .out_7(ALUSrc), .out_8(RegDst), .out_9(out_4), .out_10(ORI), .out_11(LUI),
    .out_12(Jump));
  Multiplexer #(.width(5), .disabled(0)) multiplexer_1 (
    .in0(out_2[20:16]), .in1(out_2[15:11]), .out(out_5), .sel(RegDst));  // open: en
  // Probe on out_5
  // Probe on out_6
  // Probe on out_5
  // Probe on out_2[25:21]
  GRF grf_1 (
    .in_4(out_2[25:21]), .in_5(out_2[20:16]), .in_6(out_5), .in_7(out_6), .out_8(RD1), .out_9(out_9),
    .in_1(clk), .in_2(in_1), .in_3(out_4));
  // Probe on RD1
  assign ZeroImm = {{16{1'b0}}, out_2[15:0]};  // Bit_Extender bit_extender_1
  assign SignImm = {{16{out_2[15]}}, out_2[15:0]};  // Bit_Extender bit_extender_2
  Shifter #(.width(32)) shifter_1 (.in(SignImm), .\dist (5'b10000), .out(HiImm));
  assign RORI = ZeroImm | RD1;  // OR_Gate or_1, 32 bits wide
  // Probe on ALUControl2_0
  Multiplexer #(.width(32), .disabled(0)) multiplexer_2 (
    .in0(out_9), .in1(SignImm), .out(multiplexer_2_out), .sel(ALUSrc), .en(undriven));
  ALU alu_1 (.in_2(RD1), .in_3(multiplexer_2_out), .out_4(alu_1_out_4), .out_5(out_8), .in_1(ALUControl2_0));
  and and_1 (PCSrc, Branch, alu_1_out_4);
  DataMem datamem_1 (.in_3(out_8), .in_4(out_9), .out_6(datamem_1_out_6), .in_1(clk), .in_2(out_7), .in_5(in_1));
  Multiplexer #(.width(32)) multiplexer_3 (
    .in0(out_8), .in1(datamem_1_out_6), .out(multiplexer_3_out), .sel(MemtoReg), .en(undriven_2));
  Multiplexer #(.width(32), .disabled(0)) multiplexer_4 (
    .in0(multiplexer_3_out), .in1(RORI), .out(multiplexer_4_out), .sel(ORI));  // open: en
  // Probe on out_8
  Multiplexer #(.width(32), .disabled(0)) multiplexer_5 (
    .in0(multiplexer_4_out), .in1(HiImm), .out(out_6), .sel(LUI));  // open: en

  // Other names for the same wires on the sheet: Instr[31:0] = out_2; instr15_0[15:0] = out_2[15:0];
  //   instr5_0[5:0] = out_2[5:0]; instr15_11[4:0] = out_2[15:11]; instr20_16[4:0] = out_2[20:16];
  //   instr25_21[4:0] = out_2[25:21]; instr31_26[5:0] = out_2[31:26]; MemAddr[31:0] = out_8; MemWrite = out_7;
  //   pc[31:0] = out_3; MemData[31:0] = out_9; RD2[31:0] = out_9; RegAddr[4:0] = out_5; RegData[31:0] = out_6;
  //   RegWrite = out_4; reset = in_1
endmodule

module inst_rom (
  input  [31:0] in_1,
  output [31:0] out_2
);

  wire [11:0] bit_extender_1_out;
  wire [31:0] subtractor_1_out;

  Subtractor #(.width(32)) subtractor_1 (.a(in_1), .b(32'h3000), .out(subtractor_1_out));  // open: bin, bout
  Bit_Extender #(.in_width(32), .out_width(12), .\type ("sign")) bit_extender_1 (
    .in(subtractor_1_out), .out(bit_extender_1_out));
  ROM #(.addrWidth(12), .dataWidth(32)) rom_1 (.addr(bit_extender_1_out), .data(out_2));  // open: sel

  // Other names for the same wires on the sheet: Instr[31:0] = out_2; PC[31:0] = in_1

  // Notes on the sheet:
  //   contents of rom_1 (hex, n*v repeats v):
  //   346376a3 3481488f 34846e36 ac010080 20022 ac0319fc 8c0027f8 3420431c 34a17ced 34029baf 8c051c04
  //   a40820 822822 ac0500a4 8c04235c 812820 210020 ac032ef4 200020 8c010cf4 8c051fc8 250820 8c000628
  //   432022 232822 8c040724 211820 ac010720 ac0516d4 802020 3485383f 630820 8c052d30 8c0017a8 8c040238
  //   8c001f0c 3465a1c1 8c0516e0 51822 8c021070 ac020dd0 348091b1 ac010e80 851022 34230cb1 420820 a20022
  //   211020 3403a9cb ac03119c 8c002240 a31822 640822 232020 8c001628 250820 ac010cbc ac040e18 842022
  //   412820 452020 3460037e 8c012c54 34044f40 34603c34 8c03227c ac050348 420022 8c002534 8c002ddc
  //   ac032b68 342405db 8c0026f8 8c051654 34843338 441022 840822 210822 ac040698 a41020 602822 22820
  //   8c031570 a40820 ac031be8 34a23074 612022 822822 30020 34043f73 651022 8c022d60 8c0501f0 410820 50822
  //   8c051674 442022 810822 34a5ef6f ac030478 ac020bb8 8c01178c 8c0025f4 201022 8c01041c ac0401d4 a21022
  //   3400510a a32022 812022 ac0121ec ac030d70 3461d633 ac0205ec 422820 34a34f93 ac0503e0 8c051228 222020
  //   820022 411820 8c001438 ac04180c 34858109 ac051f60 440820 8c022a74 8c051144 241822 840022 232022
  //   34409a71 ac041364 8c021ecc ac042fc4 8c031dd4 34817716 212822 840820 32020 3420ff15 250020 642022
  //   ac052720 841020 30820 ac0128f0 11022 8c0226d0 811020 401820 ac01216c 8c030db4 ac020c50 8c03290c
  //   8c0425c0 ac052ef8 ac0207ec 3464f87d ac051418 8c030334 3465f460 3444fbf9 a40820 8c051d2c 652020
  //   a42020 8c0228c8 8c02084c a41020 212020 8c021b54 8c0528ac 252022 ac0519b4 210820 344055e1 212822
  //   51822 34651cc0 8c040ebc 452822 822020 a30822 ac002528 ac022578 ac0305e0 34025a5a 8c050df0 242020
  //   ac0108d8 8c031768 8c01215c ac0505ac 8c0518c8 8c041930 610022 421020 3425dd27 8c02186c ac020568
  //   8c040b64 34a17c70 a12820 ac011d78 221822 8c03160c 8c001874 8c030b48 642820 611822 ac0110b8 232022
  //   a22820 8c0101d8 402022 442822 8c031784 346094e1 34a1d9fe ac030484 8c032050 650022 8c021ca4 ac0005bc
  //   ac0527d8 251820 631822 8c051ad8 ac042f28 822 3460569d 240022 3442e926 3405c8d6 252022 8c040490
  //   a11020 ac0116d0 ac040db4 8c032eb4 344163fc 344396c4 ac042e44 8c0010d4 3463c49c 8c020efc 431022
  //   202822 a22020 ac0318c4 821822 ac0219c0 3400dc43 8c021b2c 800022 3401a600 8c032fa4 212822 3443f31e
  //   640022 3423cff7 34815a26 211822 850020 411822 3423f29d 8c0429bc ac05178c 401820 201820 412020 402820
  //   10820 3400bfdc ac002b90 34a276f6 40820 840022 221022 3463ed2c 34a41471 ac041550 412022 ac032f54
  //   450020 632020 10022 ac00061c ac041d38 a32020 a10022 a41820 8c052234 32822 3423a0b5 450822 612820
  //   430820 801822 810022 211022 ac011184 8c000844 630822 851820 3402f214 8c0020d4 50822 3483a02a
  //   8c032ff0 ac022980 632820 230022 ac040858 820022 a32022 34a56d52 346515a7 8c040c9c 3421afbc 212020
  //   622820 8c002b1c ac041770 8c051838 a11820 451020 8c031ee4 34825170 8c001424 440820 8c012378 ac030f84
  //   ac0113a0 8c022298 8c0029c4 ac022df0 8c042cbc ac040220 632020 8c042068 250022 a41822 642820 441822
  //   ac0327c4 8c051a1c 650020 34a44127 20820 3465aa80 201022 211822 8c022de0 12820 611822 8c052b90
  //   8c040ddc ac0508b8 ac050f94 641022 ac011da4 211022 611020 51022 632020 3443ef51 3482d0ea 231822 2820
  //   8c031518 42022 430022 3462dbb4 ac000e88 ac0101a8 34a3ba6a 802020 a20022 ac022b4c 3483cb1f ac052c14
  //   8c052a88 8c011534 a41020 401822 410822 8c031770 8c010814 622022 50022 a00822 ac000a30 ac030e90
  //   ac03057c 230022 200822 34648d98 ac0320fc 842020 34040b6b 12822 52022 8c012c54 a42820 230820 450820
  //   812020 ac012e00 344009ea 652020 8c012e0c 3484f97f 34854ec1 231022 8c020b24 34015566 ac0013dc 841020
  //   a10822 a40820 ac040910 ac03009c ac02082c 34615b30 8c0306f0 34a35da3 32820 8c031c4c 831820 a21822
  //   ac042a70 642820 401022 34040ad7 8c0204b8 34618ac8 10020 a32022 8c01144c 8c012d74 ac0006a4 ac0415b4
  //   3400de17 ac040b18 30822 812820 a32022 34231241 34210a37 ac010110 ac020b4c 8c012a5c 651020 811020
  //   410022 3482ef2f 432820 8c031754 640022 641820 42022 34a1eb87 12022 3464d99e 8c022000 8c02215c
  //   8c0504b8 8c022c2c 8c001790 ac012390 ac0211e8 241022 3441d122 a21022 8c020d5c ac0429e0 800820 11820
  //   251822 631822 3401ab8f 346004d8 ac042918 451022 831022 ac040830 34a5c0b1 622022 812020 ac022b5c
  //   344053e8 ac0307c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
endmodule

module GRF (
  input  in_1,
  input  in_2,
  input  in_3,
  input  [4:0] in_4,
  input  [4:0] in_5,
  input  [4:0] in_6,
  input  [31:0] in_7,
  output [31:0] out_8,
  output [31:0] out_9
);

  wire [31:0] in_R0, in_R1, in_R2, in_R3, in_R4, in_R5, in_R6, in_R7, in_R8, in_R9, in_R10, in_R11, in_R12,
       in_R13, in_R14, in_R15, in_R16, in_R17, in_R18, in_R19, in_R20, in_R21, in_R22, in_R23, in_R24,
       in_R25, in_R26, in_R27, in_R28, in_R29, in_R30, in_R31, out_R0, out_R1, out_R2, out_R3, out_R4,
       out_R5, out_R6, out_R7, out_R8, out_R9, out_R10, out_R11, out_R12, out_R13, out_R14, out_R15, out_R16,
       out_R17, out_R18, out_R19, out_R20, out_R21, out_R22, out_R23, out_R24, out_R25, out_R26, out_R27,
       out_R28, out_R29, out_R30, out_R31;

  // Probe on in_R1
  // Probe on out_R1
  // Probe on out_8
  Multiplexer #(.select(5), .width(32)) multiplexer_1 (
    .in0(out_R0), .in1(out_R1), .in2(out_R2), .in3(out_R3), .in4(out_R4), .in5(out_R5), .in6(out_R6),
    .in7(out_R7), .in8(out_R8), .in9(out_R9), .in10(out_R10), .in11(out_R11), .in12(out_R12), .in13(out_R13),
    .in14(out_R14), .in15(out_R15), .in16(out_R16), .in17(out_R17), .in18(out_R18), .in19(out_R19),
    .in20(out_R20), .in21(out_R21), .in22(out_R22), .in23(out_R23), .in24(out_R24), .in25(out_R25),
    .in26(out_R26), .in27(out_R27), .in28(out_R28), .in29(out_R29), .in30(out_R30), .in31(out_R31),
    .out(out_8), .sel(in_4));  // open: en
  // Probe on in_4
  Register #(.width(32)) register_1 (.Q(out_R0), .clk(in_1), .clr(in_2));  // open: D, en
  Register #(.width(32)) register_2 (.D(in_R8), .Q(out_R8), .clk(in_1), .clr(in_2));  // open: en
  Register #(.width(32)) register_3 (.D(in_R16), .Q(out_R16), .clk(in_1), .clr(in_2));  // open: en
  Register #(.width(32)) register_4 (.D(in_R24), .Q(out_R24), .clk(in_1), .clr(in_2));  // open: en
  Register #(.width(32)) register_5 (.D(in_R1), .Q(out_R1), .clk(in_1), .clr(in_2));  // open: en
  Register #(.width(32)) register_6 (.D(in_R9), .Q(out_R9), .clk(in_1), .clr(in_2));  // open: en
  Register #(.width(32)) register_7 (.D(in_R17), .Q(out_R17), .clk(in_1), .clr(in_2));  // open: en
  Register #(.width(32)) register_8 (.D(in_R25), .Q(out_R25), .clk(in_1), .clr(in_2));  // open: en
  Register #(.width(32)) register_9 (.D(in_R2), .Q(out_R2), .clk(in_1), .clr(in_2));  // open: en
  Register #(.width(32)) register_10 (.D(in_R10), .Q(out_R10), .clk(in_1), .clr(in_2));  // open: en
  Register #(.width(32)) register_11 (.D(in_R18), .Q(out_R18), .clk(in_1), .clr(in_2));  // open: en
  Register #(.width(32)) register_12 (.D(in_R26), .Q(out_R26), .clk(in_1), .clr(in_2));  // open: en
  Multiplexer #(.select(5), .width(32)) multiplexer_2 (
    .in0(out_R0), .in1(out_R1), .in2(out_R2), .in3(out_R3), .in4(out_R4), .in5(out_R5), .in6(out_R6),
    .in7(out_R7), .in8(out_R8), .in9(out_R9), .in10(out_R10), .in11(out_R11), .in12(out_R12), .in13(out_R13),
    .in14(out_R14), .in15(out_R15), .in16(out_R16), .in17(out_R17), .in18(out_R18), .in19(out_R19),
    .in20(out_R20), .in21(out_R21), .in22(out_R22), .in23(out_R23), .in24(out_R24), .in25(out_R25),
    .in26(out_R26), .in27(out_R27), .in28(out_R28), .in29(out_R29), .in30(out_R30), .in31(out_R31),
    .out(out_9), .sel(in_5));  // open: en
  Register #(.width(32)) register_13 (.D(in_R3), .Q(out_R3), .clk(in_1), .clr(in_2));  // open: en
  Register #(.width(32)) register_14 (.D(in_R11), .Q(out_R11), .clk(in_1), .clr(in_2));  // open: en
  Register #(.width(32)) register_15 (.D(in_R19), .Q(out_R19), .clk(in_1), .clr(in_2));  // open: en
  Register #(.width(32)) register_16 (.D(in_R27), .Q(out_R27), .clk(in_1), .clr(in_2));  // open: en
  Register #(.width(32)) register_17 (.D(in_R4), .Q(out_R4), .clk(in_1), .clr(in_2));  // open: en
  Register #(.width(32)) register_18 (.D(in_R12), .Q(out_R12), .clk(in_1), .clr(in_2));  // open: en
  Register #(.width(32)) register_19 (.D(in_R20), .Q(out_R20), .clk(in_1), .clr(in_2));  // open: en
  Register #(.width(32)) register_20 (.D(in_R28), .Q(out_R28), .clk(in_1), .clr(in_2));  // open: en
  // Probe on in_R3
  Register #(.width(32)) register_21 (.D(in_R5), .Q(out_R5), .clk(in_1), .clr(in_2));  // open: en
  Register #(.width(32)) register_22 (.D(in_R13), .Q(out_R13), .clk(in_1), .clr(in_2));  // open: en
  Register #(.width(32)) register_23 (.D(in_R21), .Q(out_R21), .clk(in_1), .clr(in_2));  // open: en
  Register #(.width(32)) register_24 (.D(in_R29), .Q(out_R29), .clk(in_1), .clr(in_2));  // open: en
  // Probe on in_7
  // Probe on in_R1
  Demultiplexer #(.select(5), .width(32), .tristate("true")) demultiplexer_1 (
    .out0(in_R0), .out1(in_R1), .out2(in_R2), .out3(in_R3), .out4(in_R4), .out5(in_R5), .out6(in_R6),
    .out7(in_R7), .out8(in_R8), .out9(in_R9), .out10(in_R10), .out11(in_R11), .out12(in_R12), .out13(in_R13),
    .out14(in_R14), .out15(in_R15), .out16(in_R16), .out17(in_R17), .out18(in_R18), .out19(in_R19),
    .out20(in_R20), .out21(in_R21), .out22(in_R22), .out23(in_R23), .out24(in_R24), .out25(in_R25),
    .out26(in_R26), .out27(in_R27), .out28(in_R28), .out29(in_R29), .out30(in_R30), .out31(in_R31),
    .in(in_7), .sel(in_6), .en(in_3));
  // Probe on in_6
  Register #(.width(32)) register_25 (.D(in_R6), .Q(out_R6), .clk(in_1), .clr(in_2));  // open: en
  Register #(.width(32)) register_26 (.D(in_R14), .Q(out_R14), .clk(in_1), .clr(in_2));  // open: en
  Register #(.width(32)) register_27 (.D(in_R22), .Q(out_R22), .clk(in_1), .clr(in_2));  // open: en
  Register #(.width(32)) register_28 (.D(in_R30), .Q(out_R30), .clk(in_1), .clr(in_2));  // open: en
  Register #(.width(32)) register_29 (.D(in_R7), .Q(out_R7), .clk(in_1), .clr(in_2));  // open: en
  Register #(.width(32)) register_30 (.D(in_R15), .Q(out_R15), .clk(in_1), .clr(in_2));  // open: en
  Register #(.width(32)) register_31 (.D(in_R23), .Q(out_R23), .clk(in_1), .clr(in_2));  // open: en
  Register #(.width(32)) register_32 (.D(in_R31), .Q(out_R31), .clk(in_1), .clr(in_2));  // open: en

  // Other names for the same wires on the sheet: A1[4:0] = in_4; A2[4:0] = in_5; A3[4:0] = in_6; clk = in_1;
  //   RD1[31:0] = out_8; RD2[31:0] = out_9; reset = in_2; WD[31:0] = in_7; WE = in_3
endmodule

module ALU (
  input  [2:0] in_1,
  input  [31:0] in_2,
  input  [31:0] in_3,
  output out_4,
  output [31:0] out_5
);

  wire Zero;
  wire [31:0] and_1_out, AsubB, bit_extender_1_out, multiplexer_1_out, not_1_out, or_1_out;

  // Probe on in_3
  assign not_1_out = ~in_3;  // NOT_Gate not_1, 32 bits wide
  Multiplexer #(.width(32)) multiplexer_1 (
    .in0(in_3), .in1(not_1_out), .out(multiplexer_1_out), .sel(in_1[2]));  // open: en
  assign and_1_out = multiplexer_1_out & in_2;  // AND_Gate and_1, 32 bits wide
  assign or_1_out = multiplexer_1_out | in_2;  // OR_Gate or_1, 32 bits wide
  Adder #(.width(32)) adder_1 (.a(multiplexer_1_out), .b(in_2), .out(AsubB), .cin(in_1[2]));  // open: cout
  or or_2 (Zero, out_5[0], out_5[1], out_5[2], out_5[3], out_5[4], out_5[5], out_5[6], out_5[7], out_5[8], out_5[9], out_5[10], out_5[11], out_5[12], out_5[13], out_5[14], out_5[15], out_5[17], out_5[18], out_5[19], out_5[20], out_5[21], out_5[22], out_5[23], out_5[24], out_5[25], out_5[26], out_5[27], out_5[28], out_5[29], out_5[30], out_5[31], out_5[16]);
  Multiplexer #(.select(2), .width(32), .disabled(0)) multiplexer_2 (
    .in0(and_1_out), .in1(or_1_out), .in2(AsubB), .in3(bit_extender_1_out), .out(out_5), .sel(in_1[1:0]));  // open: en
  assign bit_extender_1_out = {{31{1'b0}}, AsubB[31]};  // Bit_Extender bit_extender_1
  // Probe on in_2
  // Probe on in_1[1:0]
  not not_2 (out_4, Zero);

  // Other names for the same wires on the sheet: ALUControl[2:0] = in_1; ALUControl2 = in_1[2];
  //   ALUControl1_0[1:0] = in_1[1:0]; SrcA[31:0] = in_2; SrcB[31:0] = in_3; Y[31:0] = out_5
endmodule

module DataMem (
  input  in_1,
  input  in_2,
  input  [31:0] in_3,
  input  [31:0] in_4,
  input  in_5,
  output [31:0] out_6
);

  wire not_1_out;
  wire [23:0] bit_extender_1_out;
  wire [31:0] shifter_1_out;

  // Probe on in_3
  Shifter #(.width(32), .shift("lr")) shifter_1 (.in(in_3), .\dist (5'b00010), .out(shifter_1_out));
  Bit_Extender #(.in_width(32), .out_width(24)) bit_extender_1 (.in(shifter_1_out), .out(bit_extender_1_out));
  // Probe on out_6
  not not_1 (not_1_out, in_2);
  RAM #(.addrWidth(24), .dataWidth(32), .bus("separate")) ram_1 (
    .addr(bit_extender_1_out), .din(in_4), .data(out_6), .str(in_2), .clk(in_1), .ld(not_1_out), .clr(in_5));  // open: sel

  // Other names for the same wires on the sheet: A[31:0] = in_3; clk = in_1; RD[31:0] = out_6; reset = in_5;
  //   WD[31:0] = in_4; WE = in_2
endmodule

module controler (
  input  [5:0] in_1,
  input  [5:0] in_2,
  output out_3,
  output out_4,
  output \是否为Beq指令 ,
  output [2:0] out_6,
  output out_7,
  output out_8,
  output out_9,
  output out_10,
  output out_11,
  output out_12
);

  wire [1:0] ALUOp1_0;

  MainTranslater maintranslater_1 (
    .in_1(in_1), .out_2(out_3), .out_3(out_4), .out_4(\是否为Beq指令 ), .out_5(out_7), .out_6(out_8),
    .out_7(out_9), .out_11(ALUOp1_0), .out_8(out_10), .out_9(out_11), .out_10(out_12));
  ALUTranslater alutranslater_1 (.in_2(in_2), .out_3(out_6), .in_1(ALUOp1_0));
  // Probe on out_6

  // Other names for the same wires on the sheet: ALUControl2_0[2:0] = out_6; ALUSrc = out_7; Branch = \是否为Beq指令 ;
  //   instr5_0[5:0] = in_2; instr31_26[5:0] = in_1; Jump = out_12; LUI = out_11; MemtoReg = out_3; MemWrite = out_4;
  //   ORI = out_10; RegDst = out_8; RegWrite = out_9

  // Notes on the sheet:
  //   当MemWrite为1时，写入存储器，为0时读取存储器
  //   是则为1
  //   控制进行什么ALU操作
  //   当MemtoReg为0时，将ALUResult存入寄存器；为1时，将ReadData存入寄存器
  //   ALUSrc为0时，执行R类指令，ALUSrc为1时，执行lw或sw指令
  //   当RegWrite为1时，写入寄存器文件，为0时读取寄存器文件
  //   RegWrite为1时，20：16为寄存器文件写入地址，RegWrite为0时，15：11为寄存器文件写入地址
endmodule

module MainTranslater (
  input  [5:0] in_1,
  output out_2,
  output out_3,
  output out_4,
  output out_5,
  output out_6,
  output out_7,
  output out_8,
  output out_9,
  output out_10,
  output [1:0] out_11
);

  wire andlogic_1_out_2, andlogic_1_out_3, andlogic_1_out_4, andlogic_1_out_5, andlogic_1_out_6,
       andlogic_1_out_7, andlogic_1_out_8;

  ANDLogic andlogic_1 (
    .in_1(in_1), .out_2(andlogic_1_out_2), .out_3(andlogic_1_out_3), .out_4(andlogic_1_out_4),
    .out_5(andlogic_1_out_5), .out_6(andlogic_1_out_6), .out_7(andlogic_1_out_7), .out_8(andlogic_1_out_8));
  ORLogic orlogic_1 (
    .R(andlogic_1_out_2), .ori(andlogic_1_out_3), .lw(andlogic_1_out_4), .sw(andlogic_1_out_5),
    .beq(andlogic_1_out_6), .lui(andlogic_1_out_7), .jump(andlogic_1_out_8), .out_14(out_11), .out_8(out_2),
    .out_9(out_3), .out_10(out_4), .out_11(out_5), .out_12(out_6), .out_13(out_7), .out_15(out_8),
    .out_16(out_9), .out_17(out_10));
  // Probe on out_11

  // Other names for the same wires on the sheet: ALUOp1_0[1:0] = out_11; ALUSrc = out_5; Branch = out_4;
  //   Jump = out_10; LUI = out_9; MemtoReg = out_2; MemWrite = out_3; Opcode[5:0] = in_1; ORI = out_8; RegDst = out_6;
  //   RegWrite = out_7

  // Notes on the sheet:
  //   ORLogic
endmodule

module ALUTranslater (
  input  [1:0] in_1,
  input  [5:0] in_2,
  output [2:0] out_3
);

  wire add_2_out, add_out, and_out, not_1_out, not_2_out, not_3_out, not_4_out, not_5_out, not_6_out,
       not_7_out, not_8_out, or_out, slt_out, sub_2_out, sub_out;

  not not_1 (not_1_out, in_1[1]);
  not not_2 (not_2_out, in_1[0]);
  not not_3 (not_3_out, in_2[4]);
  not not_4 (not_4_out, in_2[5]);
  not not_5 (not_5_out, in_2[2]);
  not not_6 (not_6_out, in_2[3]);
  not not_7 (not_7_out, in_2[1]);
  not not_8 (not_8_out, in_2[0]);
  and add (add_out, not_1_out, not_2_out);
  buf sub (sub_out, in_1[0]);  // AND_Gate
  and add_2 (add_2_out, in_1[1], in_2[5], not_3_out, not_6_out, not_5_out, not_7_out, not_8_out);
  and sub_2 (sub_2_out, in_1[1], in_2[5], not_3_out, not_6_out, not_5_out, in_2[1], not_8_out);
  and \and  (and_out, in_1[1], in_2[5], not_3_out, not_6_out, in_2[2], not_7_out, not_8_out);
  and \or  (or_out, in_1[1], in_2[5], not_3_out, not_6_out, in_2[2], not_7_out, in_2[0]);
  and slt (slt_out, in_1[1], in_2[5], not_3_out, in_2[3], not_5_out, in_2[1], not_8_out);
  or or_2 (out_3[2], sub_out, sub_2_out, slt_out);
  or or_3 (out_3[1], add_out, sub_out, add_2_out, sub_2_out, slt_out);
  or or_4 (out_3[0], slt_out, or_out);

  // Other names for the same wires on the sheet: ALUControl[2:0] = out_3; ALUControl0 = out_3[0];
  //   ALUControl1 = out_3[1]; ALUControl2 = out_3[2]; ALUOp[1:0] = in_1; ALUOp0 = in_1[0]; ALUOp1 = in_1[1];
  //   funct[5:0] = in_2; op0 = in_2[0]; op1 = in_2[1]; op2 = in_2[2]; op3 = in_2[3]; op4 = in_2[4]; op5 = in_2[5]
endmodule

module ANDLogic (
  input  [5:0] in_1,
  output out_2,
  output out_3,
  output out_4,
  output out_5,
  output out_6,
  output out_7,
  output out_8
);

  wire not_1_out, not_2_out, not_3_out, not_4_out, not_5_out, not_6_out;

  not not_1 (not_1_out, in_1[5]);
  not not_2 (not_2_out, in_1[4]);
  not not_3 (not_3_out, in_1[3]);
  not not_4 (not_4_out, in_1[2]);
  not not_5 (not_5_out, in_1[0]);
  not not_6 (not_6_out, in_1[1]);
  and R (out_2, not_1_out, not_2_out, not_3_out, not_4_out, not_6_out, not_5_out);
  and ori (out_3, not_1_out, not_2_out, in_1[3], in_1[2], not_6_out, in_1[0]);
  and lw (out_4, in_1[5], not_2_out, not_3_out, not_4_out, in_1[1], in_1[0]);
  and sw (out_5, in_1[5], not_2_out, in_1[3], not_4_out, in_1[1], in_1[0]);
  and beq (out_6, not_1_out, not_2_out, not_3_out, in_1[2], not_6_out, not_5_out);
  and lui (out_7, not_1_out, not_2_out, in_1[3], in_1[2], in_1[1], in_1[0]);
  and jump (out_8, not_1_out, not_2_out, not_3_out, not_4_out, in_1[1], not_5_out);

  // Other names for the same wires on the sheet: instr31_26[5:0] = in_1; op0 = in_1[0]; op1 = in_1[1]; op2 = in_1[2];
  //   op3 = in_1[3]; op4 = in_1[4]; op5 = in_1[5]
endmodule

module ORLogic (
  input  R,
  input  ori,
  input  lw,
  input  sw,
  input  beq,
  input  lui,
  input  jump,
  output out_8,
  output out_9,
  output out_10,
  output out_11,
  output out_12,
  output out_13,
  output [1:0] out_14,
  output out_15,
  output out_16,
  output out_17
);

  or or_1 (out_13, lw, R, ori, lui);
  buf or_2 (out_12, R);  // OR_Gate
  or or_3 (out_11, lw, sw, lw);
  buf or_4 (out_10, beq);  // OR_Gate
  buf or_5 (out_9, sw);  // OR_Gate
  buf or_6 (out_8, lw);  // OR_Gate
  buf or_7 (out_14[1], R);  // OR_Gate
  buf or_8 (out_14[0], beq);  // OR_Gate
  buf or_9 (out_15, ori);  // OR_Gate
  buf or_10 (out_16, lui);  // OR_Gate
  buf or_11 (out_17, jump);  // OR_Gate

  // Other names for the same wires on the sheet: ALUOp0 = out_14[0]; ALUOp1_0[1:0] = out_14; ALUOp1 = out_14[1];
  //   ALUSrc = out_11; Branch = out_10; jump_t = out_17; LUI_t = out_16; MemtoReg = out_8; MemWrite = out_9;
  //   ORI_t = out_15; RegDst = out_12; RegWrite = out_13
endmodule

module ALUANDLogic (
  input  [1:0] in_1,
  input  [5:0] in_2,
  output out_3,
  output out_4,
  output out_5,
  output out_6,
  output out_7,
  output out_8
);

  wire not_1_out, not_2_out, not_3_out, not_4_out, not_5_out, not_6_out, not_7_out, not_8_out;

  not not_1 (not_1_out, in_1[1]);
  not not_2 (not_2_out, in_1[0]);
  not not_3 (not_3_out, in_2[5]);
  not not_4 (not_4_out, in_2[4]);
  not not_5 (not_5_out, in_2[2]);
  not not_6 (not_6_out, in_2[3]);
  not not_7 (not_7_out, in_2[1]);
  not not_8 (not_8_out, in_2[0]);
  and add (out_3, in_2[5], not_4_out, not_6_out, not_5_out, not_7_out, not_8_out);
  and sub (out_4, in_2[5], not_4_out, not_6_out, not_5_out, in_2[1], not_8_out);
  and \and  (out_5, in_2[5], not_4_out, not_6_out, in_2[2], not_7_out, not_8_out);
  and \or  (out_6, in_2[5], not_4_out, not_6_out, in_2[2], not_7_out, in_2[0]);
  and slt (out_7, in_2[5], not_4_out, in_2[3], not_5_out, in_2[1], not_8_out);
  and and_2 (out_8, not_3_out, not_4_out, in_2[3], in_2[2], in_2[1], in_2[0]);

  // Other names for the same wires on the sheet: ALUOp[1:0] = in_1; ALUOp0 = in_1[0]; ALUOp1 = in_1[1];
  //   funct[5:0] = in_2; op0 = in_2[0]; op1 = in_2[1]; op2 = in_2[2]; op3 = in_2[3]; op4 = in_2[4]; op5 = in_2[5]
endmodule

module ALUORLogic (
  input  add,
  input  sub,
  input  \and ,
  input  \or ,
  input  slt,
  input  in_6
);

  wire ALUControl0, ALUControl1, ALUControl2;

  // OR_Gate or_1 has open pins: out=ALUControl2
  // OR_Gate or_2 has open pins: out=ALUControl1
  // OR_Gate or_3 has open pins: out=ALUControl0
endmodule

module IFU (
  input  in_1,
  input  in_2,
  input  in_3,
  input  in_4,
  output [31:0] out_5,
  output [31:0] out_6
);

  wire [31:0] bit_extender_1_out, multiplexer_1_out, multiplexer_2_out, PC_q, PCBranch, PCPlus4,
       shifter_1_out, xor_1_out;

  Multiplexer #(.width(32)) multiplexer_1 (
    .in0(PCPlus4), .in1(PCBranch), .out(multiplexer_1_out), .sel(in_3));  // open: en
  assign xor_1_out = 32'h3000 ^ multiplexer_2_out;  // XOR_Gate xor_1, 32 bits wide
  Multiplexer #(.width(32)) multiplexer_2 (
    .in0(multiplexer_1_out), .in1({out_5[31:28], out_6[25:0], 2'b00}), .out(multiplexer_2_out), .sel(in_4));  // open: en
  Register #(.width(32)) PC (.D(xor_1_out), .Q(PC_q), .clk(in_2), .clr(in_1));  // open: en
  assign out_5 = 32'h3000 ^ PC_q;  // XOR_Gate xor_2, 32 bits wide
  IM im_1 (.in_1(out_5), .out_2(out_6));
  Adder #(.width(32)) adder_1 (.a(out_5), .b(32'h4), .out(PCPlus4));  // open: cin, cout
  assign bit_extender_1_out = {{16{out_6[15]}}, out_6[15:0]};  // Bit_Extender bit_extender_1
  Shifter #(.width(32)) shifter_1 (.in(bit_extender_1_out), .\dist (5'b00010), .out(shifter_1_out));
  Adder #(.width(32)) adder_2 (.a(shifter_1_out), .b(PCPlus4), .out(PCBranch));  // open: cin, cout

  // Other names for the same wires on the sheet: Instr[31:0] = out_6; instr5_0[5:0] = out_6[5:0];
  //   instr15_0[15:0] = out_6[15:0]; instr15_11[4:0] = out_6[15:11]; instr20_16[4:0] = out_6[20:16];
  //   instr25_21[4:0] = out_6[25:21]; pc[31:0] = out_5; clk = in_2; instr31_26[5:0] = out_6[31:26]; Jump = in_4;
  //   PCSrc = in_3; reset = in_1
endmodule

module IM (
  input  [31:0] in_1,
  output [31:0] out_2
);

  wire [11:0] bit_extender_1_out;
  wire [31:0] divider_1_out, subtractor_1_out;

  // Probe on in_1
  // Probe on subtractor_1_out
  Subtractor #(.width(32)) subtractor_1 (.a(in_1), .b(32'h3000), .out(subtractor_1_out));  // open: bin, bout
  Bit_Extender #(.in_width(32), .out_width(12), .\type ("sign")) bit_extender_1 (
    .in(divider_1_out), .out(bit_extender_1_out));
  Divider #(.width(32)) divider_1 (.a(subtractor_1_out), .b(32'h4), .out(divider_1_out));  // open: upper, rem
  // Probe on divider_1_out
  // Probe on bit_extender_1_out
  ROM #(.addrWidth(12), .dataWidth(32)) rom_1 (.addr(bit_extender_1_out), .data(out_2));  // open: sel
  // Probe on out_2

  // Other names for the same wires on the sheet: Instr[31:0] = out_2; PC[31:0] = in_1

  // Notes on the sheet:
  //   contents of rom_1 (hex, n*v repeats v):
  //   3421cdc2 831020 250820 3484960e 602022 222822 412820 242822 342326c9 830020 642822 852022 200820
  //   a40022 34850a5e 22 811022 251820 640020 3402df3e 640820 3463ac4c 52820 20 34004e32 346052a2 432822
  //   3444290f 34a2abc6 3405db60 211022 34a4188c 432822 3444c2a4 621020 3420ef74 34617b4f 851820 34a56bf8
  //   621822 850022 3483998e 800022 830022 3442184c a30820 412820 200820 32022 3463920c 802822 3485feb5
  //   222822 242822 3442f765 34a4d04d 801820 31020 650820 34601f48 610822 a11020 3423a65a 34a3c8fe 401822
  //   34a4a57b 402820 450022 41022 3480020e 412822 34008c6d 212022 a42822 250022 830822 3484a01c 34a5e5fd
  //   11820 34058a89 610820 34a248d0 641020 822022 41022 441020 3482e3fb 42022 a12822 30820 812820 222822
  //   34231e42 34453119 220020 34623474 34a46186 611820 32820 221022 34433068 3484b382 452822 a41022
  //   a00020 820022 3401cd92 34058443 801020 1020 611820 34457700 430820 601020 640820 34403dd6 34800594
  //   a32022 30820 651820 34a12462 841020 51820 34034f80 a51020 10022 a12820 3460efe6 12020 3443e18e
  //   411820 3425abcc 231822 800820 431022 3420432a 830022 a01820 421022 802820 410020 34023c57 a01822
  //   240022 3440d9f8 a31820 34221b52 a10822 12822 346399d8 812822 34011293 3440f9fd 12022 34a5d4f7 a12022
  //   612020 810820 a11822 411020 821820 342307fe 831020 22022 348336a2 34820f34 3421ac2e 34040954 822
  //   3424ed9a 3401e8ca 602820 41820 a31020 34659b3c 811020 802020 252820 3424844b 802022 630020 632820
  //   10820 3483cf7d 34443f7b a42022 3425323a 621822 800820 200820 52020 621822 811020 3441bfff 34607ade
  //   3425ac35 211822 a42820 a11820 348215df 210822 811822 34809254 a10020 21820 202822 610022 34a3d0ed
  //   40020 34603749 34a547f5 3460b3dc 630022 34038c71 3464f949 a30020 34a5a7ec 34256330 42022 34042b07
  //   34208d14 a52020 850020 452020 230820 601020 452822 840822 3442c959 3424bcc0 201820 21822 a41820
  //   241820 34231ee4 820020 240022 222022 822822 51822 34615bc0 3460689f 612820 31020 230820 3420ab35
  //   241022 210022 420020 252022 34a306ee 3482f1f8 232020 840822 a21022 821022 34a47a4e 840022 252022
  //   34648727 a11822 612820 34a40cd8 241820 452820 34046d90 641022 620022 242020 421022 640822 34210952
  //   3464d27c 34a06da8 22022 a32822 401022 34655926 34854371 3425fdf1 650820 831820 430820 22820 34a5357a
  //   34a035ac 251020 621020 850020 34837a11 34a31375 a42022 650822 432020 401820 212820 34837541 a52820
  //   a20022 3425cd53 231820 852820 252822 3484c70a 820022 831022 611020 34a1942c 34a0c25e a32820 602822
  //   3400971b 3424853a 651820 851822 422022 3485a411 3441cd2c 34435a2d 34848f07 801822 432020 a01822
  //   a00820 41020 3421106b 630822 201820 652822 221020 340262d5 452022 612820 821022 222822 34806880
  //   34a25b88 241822 430020 430020 251022 3404253e 20822 251820 201020 30820 620022 840820 621820 812822
  //   41022 a01022 34043d0d 34015b4b 34056206 34643e54 a51022 a21020 652822 812820 631022 51820 34422ec2
  //   610020 20022 220820 602020 810822 34a2fb74 612020 220020 832820 220022 441822 810020 220022 34647392
  //   3483dc74 3401d419 3440f809 441822 402822 440022 2020 a30822 640820 3440e3cf 411022 201022 3464549f
  //   430020 34a5be9c 611822 400022 801020 242020 34a367f3 402822 34419dc2 a00822 3402adf9 342037c2 a20022
  //   401820 40022 a40022 641820 12820 832820 34a5269d 841022 410820 832020 451022 34a2f813 631020 a40020
  //   451022 a00022 34a458b4 231822 51022 822 a00820 402022 3402cde7 a52822 3462f342 346145f3 410822
  //   842022 851820 212022 3442596c 242822 802022 a21822 34a26a9b 400020 442022 200022 251822 210022
  //   34852506 600820 34218eef 820020 34452d68 34a45905 401022 34a3bd55 220822 210020 212820 621022 30820
  //   34a3db8a 201822 11822 800820 412820 34a208cd 810020 612022 421020 811020 601022 31820 222822 211022
  //   612822 1020 830020 a30822 a22820 821820 452822 210822 822022 3441481d 200820 852820 642020 441820
  //   41022 a42020 821022 20820 34226d05 812822 240822 a20820 34a04c4f a52020 232822 3463c534 421822
  //   432020 800022 3481c597
endmodule

module \少用tunnel  (
  input  in_1,
  output [31:0] out_2,
  output [31:0] out_3,
  output out_4,
  output [4:0] out_5,
  output [31:0] out_6,
  output out_7,
  output [31:0] out_8,
  output [31:0] out_9
);

  wire ALUSrc, Branch, clock_1_out, LUI, MemtoReg, ORI, RegDst;
  wire [2:0] ALUControl2_0;
  wire [4:0] instr20_16, instr25_21, multiplexer_1_out;
  wire [5:0] instr5_0, instr31_26;
  wire [15:6] instr15_0;

  Clock clock_1 (.out(clock_1_out));
  IFU ifu_1 (
    .in_1(in_1), .in_2(clock_1_out), .out_6({instr31_26, instr25_21, instr20_16, instr15_0, instr5_0}));  // open: in_3, out_5, in_4
  controler controler_1 (
    .in_1(instr31_26), .in_2(instr5_0), .out_3(MemtoReg), .out_4(out_7), .\是否为Beq指令 (Branch),
    .out_6(ALUControl2_0), .out_7(ALUSrc), .out_8(RegDst), .out_9(out_4), .out_10(ORI), .out_11(LUI));  // open: out_12
  GRF grf_1 (
    .in_4(instr25_21), .in_5(instr20_16), .in_6(multiplexer_1_out));  // open: in_7, out_8, out_9, in_1, in_2, in_3
  Multiplexer #(.width(5)) multiplexer_1 (
    .in0(instr20_16), .in1(instr15_0[15:11]), .out(multiplexer_1_out), .sel(RegDst));  // open: en

  // Other names for the same wires on the sheet: instr[31:0] = out_2; instr15_0[5:0] = instr5_0;
  //   instr15_11[4:0] = instr15_0[15:11]; MemAddr[31:0] = out_8; MemData[31:0] = out_9; MemWrite = out_7;
  //   pc[31:0] = out_3; RegAddr[4:0] = out_5; RegData[31:0] = out_6; RegWrite = out_4; reset = in_1
endmodule

module \补码器  (
  input  [31:0] in_1,
  output [31:0] out_2
);

  wire [31:0] adder_1_out, negator_1_out;

  Negator #(.width(32)) negator_1 (.in(in_1), .out(negator_1_out));
  Adder #(.width(32)) adder_1 (.a(negator_1_out), .b(32'h1), .out(adder_1_out));  // open: cin, cout
  Multiplexer #(.width(32)) multiplexer_1 (.in0(in_1), .in1(adder_1_out), .out(out_2), .sel(in_1[31]));  // open: en

  // Other names for the same wires on the sheet: sign = in_1[31]
endmodule

module test (
  input  in_1
);

  wire main_1_out_4, main_1_out_7;
  wire [4:0] main_1_out_5;
  wire [31:0] main_1_out_2, main_1_out_3, main_1_out_6, main_1_out_8, main_1_out_9;

  main main_1 (
    .in_1(in_1), .out_2(main_1_out_2), .out_3(main_1_out_3), .out_4(main_1_out_4), .out_5(main_1_out_5),
    .out_6(main_1_out_6), .out_7(main_1_out_7), .out_8(main_1_out_8), .out_9(main_1_out_9));
endmodule

module copy (
  input  in_1,
  output [31:0] out_2,
  output [31:0] out_3,
  output out_4,
  output [4:0] out_5,
  output [31:0] out_6,
  output out_7,
  output [31:0] out_8,
  output [31:0] out_9
);

  wire alu_1_out_4, ALUSrc, Branch, clk, Jump, LUI, MemtoReg, ORI, PCSrc, RegDst, undriven, undriven_2;
  wire [2:0] ALUControl2_0;
  wire [31:0] datamem_1_out_6, HiImm, multiplexer_2_out, multiplexer_3_out, multiplexer_4_out, RD1, RORI,
       SignImm, ZeroImm;

  Clock clock_1 (.out(clk));
  IFU ifu_1 (.in_1(in_1), .in_2(clk), .in_3(PCSrc), .out_5(out_3), .out_6(out_2), .in_4(Jump));
  // Probe on out_3
  // Probe on out_2[31:26]
  // Probe on out_2
  controler controler_1 (
    .in_1(out_2[31:26]), .in_2(out_2[5:0]), .out_3(MemtoReg), .out_4(out_7), .\是否为Beq指令 (Branch),
    .out_6(ALUControl2_0), .out_7(ALUSrc), .out_8(RegDst), .out_9(out_4), .out_10(ORI), .out_11(LUI),
    .out_12(Jump));
  Multiplexer #(.width(5), .disabled(0)) multiplexer_1 (
    .in0(out_2[20:16]), .in1(out_2[15:11]), .out(out_5), .sel(RegDst));  // open: en
  // Probe on out_5
  // Probe on out_6
  // Probe on out_5
  // Probe on out_2[25:21]
  GRF grf_1 (
    .in_4(out_2[25:21]), .in_5(out_2[20:16]), .in_6(out_5), .in_7(out_6), .out_8(RD1), .out_9(out_9),
    .in_1(clk), .in_2(in_1), .in_3(out_4));
  // Probe on RD1
  assign ZeroImm = {{16{1'b0}}, out_2[15:0]};  // Bit_Extender bit_extender_1
  assign SignImm = {{16{out_2[15]}}, out_2[15:0]};  // Bit_Extender bit_extender_2
  Shifter #(.width(32)) shifter_1 (.in(SignImm), .\dist (5'b10000), .out(HiImm));
  assign RORI = ZeroImm | RD1;  // OR_Gate or_1, 32 bits wide
  // Probe on ALUControl2_0
  Multiplexer #(.width(32), .disabled(0)) multiplexer_2 (
    .in0(out_9), .in1(SignImm), .out(multiplexer_2_out), .sel(ALUSrc), .en(undriven));
  ALU alu_1 (.in_2(RD1), .in_3(multiplexer_2_out), .out_4(alu_1_out_4), .out_5(out_8), .in_1(ALUControl2_0));
  and and_1 (PCSrc, Branch, alu_1_out_4);
  DataMem datamem_1 (.in_3(out_8), .in_4(out_9), .out_6(datamem_1_out_6), .in_1(clk), .in_2(out_7), .in_5(in_1));
  Multiplexer #(.width(32)) multiplexer_3 (
    .in0(out_8), .in1(datamem_1_out_6), .out(multiplexer_3_out), .sel(MemtoReg), .en(undriven_2));
  Multiplexer #(.width(32), .disabled(0)) multiplexer_4 (
    .in0(multiplexer_3_out), .in1(RORI), .out(multiplexer_4_out), .sel(ORI));  // open: en
  // Probe on out_8
  Multiplexer #(.width(32), .disabled(0)) multiplexer_5 (
    .in0(multiplexer_4_out), .in1(HiImm), .out(out_6), .sel(LUI));  // open: en

  // Other names for the same wires on the sheet: Instr[31:0] = out_2; instr5_0[5:0] = out_2[5:0];
  //   instr15_0[15:0] = out_2[15:0]; instr15_11[4:0] = out_2[15:11]; instr20_16[4:0] = out_2[20:16];
  //   instr25_21[4:0] = out_2[25:21]; instr31_26[5:0] = out_2[31:26]; MemAddr[31:0] = out_8; MemWrite = out_7;
  //   pc[31:0] = out_3; MemData[31:0] = out_9; RD2[31:0] = out_9; RegAddr[4:0] = out_5; RegData[31:0] = out_6;
  //   RegWrite = out_4; reset = in_1
endmodule

module ext (
  input  [15:0] in_1
);

  wire [31:0] bit_extender_1_out;

  assign bit_extender_1_out = {{16{in_1[15]}}, in_1};  // Bit_Extender bit_extender_1
  // Probe on bit_extender_1_out
endmodule
