// Logisim project testBench.circ as structural Verilog: 1 circuit, main circuit main
module main (
  input  in_1,
  output [31:0] out_2,
  output halt,
  output [31:0] out_4,
  output out_5,
  output [4:0] out_6,
  output [31:0] out_7,
  output out_8,
  output [31:0] out_9,
  output [31:0] out_10
);

  wire Clk;

  Clock clock_1 (.out(Clk));
  Empty_CPU_main main_1 (
    .in_1(in_1), .out_2(out_2), .out_3(out_4), .out_4(out_5), .out_5(out_6), .out_6(out_7), .out_7(out_8),
    .out_8(out_9), .out_9(out_10));
  Comparator #(.width(32)) comparator_1 (.a(out_2), .b(32'h1000ffff), .eq(halt));  // open: gt, lt
endmodule
