// Logisim project CRC校验.circ as structural Verilog: 3 circuits, main circuit main
module main (
  input  [7:0] in_1,
  input  [3:0] in_2,
  output [10:0] out_3
);

  wire [2:0] n4bitmol2_1_out_3, n4bitmol2_2_out_3, n4bitmol2_3_out_3;
  wire [3:1] n4bitmol2_4_out_3;

  // Probe on in_1[7]
  _4bitMol2 u_4bitmol2_1 (.A(in_1[7:4]), .B(in_2), .out_3(n4bitmol2_1_out_3));
  // Probe on n4bitmol2_1_out_3
  _4bitMol2 u_4bitmol2_2 (.A({n4bitmol2_1_out_3, in_1[3]}), .B(in_2), .out_3(n4bitmol2_2_out_3));
  _4bitMol2 u_4bitmol2_3 (.A({n4bitmol2_2_out_3, in_1[2]}), .B(in_2), .out_3(n4bitmol2_3_out_3));
  _4bitMol2 u_4bitmol2_4 (.A({n4bitmol2_3_out_3, in_1[1]}), .B(in_2), .out_3(n4bitmol2_4_out_3));
  _4bitMol2 u_4bitmol2_5 (.A({n4bitmol2_4_out_3, in_1[0]}), .B(in_2), .out_3(out_3[2:0]));

  assign out_3[10:3] = in_1;

  // Other names for the same wires on the sheet: A[7:0] = in_1; A3 = in_1[3]; C[10:0] = {in_1, out_3[2:0]};
  //   A2 = in_1[2]; A1 = in_1[1]; A0 = in_1[0]; B[3:0] = in_2; remainder[2:0] = out_3[2:0]; A7654[3:0] = in_1[7:4]
endmodule

module _4bitMol2 (
  input  [3:0] A,
  input  [3:0] B,
  output [2:0] out_3
);

  wire not_1_out;
  wire [3:0] multiplexer_1_out, xor_1_out;

  not not_1 (not_1_out, A[3]);
  assign xor_1_out = A ^ B;  // XOR_Gate xor_1, 4 bits wide
  // Probe on A
  // Probe on xor_1_out
  Multiplexer #(.width(4)) multiplexer_1 (
    .in0(xor_1_out), .in1(A), .out(multiplexer_1_out), .sel(not_1_out));  // open: en
  // Probe on multiplexer_1_out
  Bit_Extender #(.in_width(4), .out_width(3)) bit_extender_1 (.in(multiplexer_1_out), .out(out_3));
endmodule

module CRC (
  input  [7:0] in_1,
  input  [3:0] in_2,
  output [10:0] out_3
);

  wire [2:0] n4bitmol2_1_out_3, n4bitmol2_2_out_3, n4bitmol2_3_out_3, n4bitmol2_5_out_3, n4bitmol2_6_out_3;
  wire [3:1] n4bitmol2_4_out_3, n4bitmol2_7_out_3;

  // Probe on in_1[7]
  // Probe on in_1[7:4]
  _4bitMol2 u_4bitmol2_1 (.A(in_1[7:4]), .B(in_2), .out_3(n4bitmol2_1_out_3));
  // Probe on n4bitmol2_1_out_3
  // Probe on {n4bitmol2_1_out_3, in_1[3]}
  _4bitMol2 u_4bitmol2_2 (.A({n4bitmol2_1_out_3, in_1[3]}), .B(in_2), .out_3(n4bitmol2_2_out_3));
  // Probe on {n4bitmol2_2_out_3, in_1[2]}
  _4bitMol2 u_4bitmol2_3 (.A({n4bitmol2_2_out_3, in_1[2]}), .B(in_2), .out_3(n4bitmol2_3_out_3));
  // Probe on {n4bitmol2_3_out_3, in_1[1]}
  _4bitMol2 u_4bitmol2_4 (.A({n4bitmol2_3_out_3, in_1[1]}), .B(in_2), .out_3(n4bitmol2_4_out_3));
  // Probe on {n4bitmol2_4_out_3, in_1[0]}
  // Probe on {n4bitmol2_5_out_3, 1'b0}
  _4bitMol2 u_4bitmol2_5 (.A({n4bitmol2_4_out_3, in_1[0]}), .B(in_2), .out_3(n4bitmol2_5_out_3));
  _4bitMol2 u_4bitmol2_6 (.A({n4bitmol2_5_out_3, 1'b0}), .B(in_2), .out_3(n4bitmol2_6_out_3));
  // Probe on {n4bitmol2_7_out_3, 1'b0}
  // Probe on {n4bitmol2_6_out_3, 1'b0}
  _4bitMol2 u_4bitmol2_7 (.A({n4bitmol2_6_out_3, 1'b0}), .B(in_2), .out_3(n4bitmol2_7_out_3));
  _4bitMol2 u_4bitmol2_8 (.A({n4bitmol2_7_out_3, 1'b0}), .B(in_2), .out_3(out_3[2:0]));

  assign out_3[10:3] = in_1;

  // Other names for the same wires on the sheet: A[7:0] = in_1; A3 = in_1[3]; C[10:0] = {in_1, out_3[2:0]};
  //   A2 = in_1[2]; A1 = in_1[1]; A0 = in_1[0]; B[3:0] = in_2; remainder[2:0] = out_3[2:0]; A7654[3:0] = in_1[7:4]
endmodule
