// Logisim project fsm.circ as structural Verilog: 4 circuits, main circuit main
module main (
  input  in_1,
  input  [1:0] in_2,
  output Z
);

  wire and_1_out, clock_1_out;
  wire [1:0] register_1_q, \状态转移_1_b_2 ;

  \状态转移  \u_状态转移_1  (
    .A(register_1_q[1]), .B(register_1_q[0]), .C(in_2[1]), .D(in_2[0]), .A_2(\状态转移_1_b_2 [1]),
    .B_2(\状态转移_1_b_2 [0]));
  Clock clock_1 (.out(clock_1_out));
  Register #(.width(2)) register_1 (
    .D(\状态转移_1_b_2 ), .Q(register_1_q), .clk(clock_1_out), .clr(and_1_out));  // open: en
  and and_1 (and_1_out, clock_1_out, in_1);
  Multiplexer #(.select(2)) multiplexer_1 (
    .in0(1'b0), .in1(1'b0), .in2(1'b0), .in3(1'b1), .out(Z), .sel(\状态转移_1_b_2 ));  // open: en

  // Other names for the same wires on the sheet: CLR = in_1; In[1:0] = in_2
endmodule

module fsm (
  input  in_1,
  input  [1:0] in_2,
  output Z
);

  wire clock_1_out;
  wire [1:0] multiplexer_1_out, register_1_q, \状态转移_1_b_2 , \输出逻辑_1_b_2 ;

  \状态转移  \u_状态转移_1  (
    .A(register_1_q[1]), .B(register_1_q[0]), .C(in_2[1]), .D(in_2[0]), .A_2(\状态转移_1_b_2 [1]),
    .B_2(\状态转移_1_b_2 [0]));
  Multiplexer #(.width(2)) multiplexer_1 (
    .in0(\状态转移_1_b_2 ), .in1(2'b00), .out(multiplexer_1_out), .sel(in_1));  // open: en
  Clock clock_1 (.out(clock_1_out));
  Register #(.width(2)) register_1 (.D(multiplexer_1_out), .Q(register_1_q), .clk(clock_1_out));  // open: en, clr
  \输出逻辑  \u_输出逻辑_1  (
    .A(register_1_q[1]), .B(register_1_q[0]), .C(in_2[1]), .D(in_2[0]), .A_2(\输出逻辑_1_b_2 [1]),
    .B_2(\输出逻辑_1_b_2 [0]));
  // Probe on \输出逻辑_1_b_2 
  Multiplexer #(.select(2)) multiplexer_2 (
    .in0(1'b0), .in1(1'b0), .in2(1'b0), .in3(1'b1), .out(Z), .sel(\输出逻辑_1_b_2 ));  // open: en

  // Other names for the same wires on the sheet: CLR = in_1; In[1:0] = in_2
endmodule

module \状态转移  (
  input  A,
  input  B,
  input  C,
  input  D,
  output A_2,
  output B_2
);

  wire and_1_out, and_2_out, and_3_out, and_4_out, and_5_out, and_6_out, and_7_out, not_1_out, not_2_out,
       not_3_out, not_4_out, not_5_out, not_6_out, not_7_out;

  not not_1 (not_1_out, A);
  and and_1 (and_1_out, not_1_out, B);
  not not_2 (not_2_out, D);
  and and_2 (and_2_out, A, not_3_out);
  not not_3 (not_3_out, B);
  not not_4 (not_4_out, D);
  not not_5 (not_5_out, C);
  and and_3 (and_3_out, A, not_6_out);
  not not_6 (not_6_out, B);
  not not_7 (not_7_out, D);
  and and_4 (and_4_out, and_1_out, not_2_out);
  and and_5 (and_5_out, and_2_out, not_4_out);
  and and_6 (and_6_out, not_5_out, D);
  and and_7 (and_7_out, and_3_out, not_7_out);
  or or_1 (A_2, and_4_out, and_5_out);
  or or_2 (B_2, and_6_out, and_7_out);
endmodule

module \输出逻辑  (
  input  A,
  input  B,
  input  C,
  input  D,
  output A_2,
  output B_2
);

  wire and_1_out, and_2_out, and_3_out, and_4_out, and_5_out, and_6_out, and_7_out, not_1_out, not_2_out,
       not_3_out, not_4_out, not_5_out, not_6_out, not_7_out;

  not not_1 (not_1_out, A);
  and and_1 (and_1_out, not_1_out, B);
  not not_2 (not_2_out, D);
  and and_2 (and_2_out, A, not_3_out);
  not not_3 (not_3_out, B);
  not not_4 (not_4_out, D);
  not not_5 (not_5_out, C);
  and and_3 (and_3_out, A, not_6_out);
  not not_6 (not_6_out, B);
  not not_7 (not_7_out, D);
  and and_4 (and_4_out, and_1_out, not_2_out);
  and and_5 (and_5_out, and_2_out, not_4_out);
  and and_6 (and_6_out, not_5_out, D);
  and and_7 (and_7_out, and_3_out, not_7_out);
  or or_1 (A_2, and_4_out, and_5_out);
  or or_2 (B_2, and_6_out, and_7_out);
endmodule
