// Logisim project ftoi.circ as structural Verilog
module ftoi (
  input  [15:0] in_1,
  output [31:0] out_2
);

  wire and_1_out, not_1_out, not_3_out, or_1_out, or_2_out;
  wire [4:0] bit_extender_3_out, E;
  wire [10:0] bit_extender_1_out;
  wire [30:0] bit_extender_2_out, not_2_out, shifter_1_out, shifter_2_out;
  wire [31:0] adder_1_out, \output ;

  assign bit_extender_1_out = {{1{1'b1}}, in_1[9:0]};  // Bit_Extender bit_extender_1
  assign bit_extender_2_out = {{20{1'b0}}, bit_extender_1_out};  // Bit_Extender bit_extender_2
  assign bit_extender_3_out = {{1{1'b0}}, E[3:0]};  // Bit_Extender bit_extender_3
  // Probe on E
  Subtractor #(.width(5)) subtractor_1 (.a(in_1[14:10]), .b(5'b01111), .out(E));  // open: bin, bout
  Shifter #(.width(31)) shifter_1 (.in(bit_extender_2_out), .\dist (bit_extender_3_out), .out(shifter_1_out));
  and and_1 (and_1_out, in_1[10], in_1[11], in_1[12], in_1[13], in_1[14]);
  not not_1 (not_1_out, or_1_out);
  or or_1 (or_1_out, in_1[10], in_1[11], in_1[12], in_1[13], in_1[14]);
  Shifter #(.width(31), .shift("lr")) shifter_2 (.in(shifter_1_out), .\dist (5'b01010), .out(shifter_2_out));
  or or_2 (or_2_out, E[4], and_1_out, not_1_out);
  assign not_2_out = ~shifter_2_out;  // NOT_Gate not_2, 31 bits wide
  Multiplexer #(.width(32)) multiplexer_1 (.in0(\output ), .in1({32{1'b0}}), .out(out_2), .sel(or_2_out));  // open: en
  Adder #(.width(32)) adder_1 (.a({in_1[15], not_2_out}), .b(32'h1), .out(adder_1_out));  // open: cin, cout
  Multiplexer #(.width(32)) multiplexer_2 (
    .in0(adder_1_out), .in1({in_1[15], shifter_2_out}), .out(\output ), .sel(not_3_out));  // open: en
  not not_3 (not_3_out, in_1[15]);

  // Other names for the same wires on the sheet: sign = in_1[15]; val_E[3:0] = E[3:0]; sign_E = E[4];
  //   fraction[9:0] = in_1[9:0]; exponent[4:0] = in_1[14:10]
endmodule
