// Logisim project learnLogisim.circ as structural Verilog: 1 circuit, main circuit main
module main (
  input  [7:0] in_1,
  input  [5:0] in_2,
  input  [7:0] in_3,
  input  [3:0] in_4,
  output [3:0] out_5,
  output [15:0] out_6,
  output [3:0] out_7
);

  wire [2:0] xnor_1_out;
  wire [3:0] bit_extender_1_out, negator_1_out, shifter_1_out;

  // Probe on bit_extender_1_out
  assign bit_extender_1_out = {{2{1'b1}}, 2'b10};  // Bit_Extender bit_extender_1
  // Probe on in_1[3:0]
  // Probe on in_1[7:4]
  // Probe on shifter_1_out
  assign out_5 = in_1[3:0] & in_1[7:4];  // AND_Gate and_1, 4 bits wide
  assign xnor_1_out = ~(in_2[2:0] ^ in_2[5:3]);  // XNOR_Gate xnor_1, 3 bits wide
  assign out_6 = {{8{in_3[7]}}, in_3};  // Bit_Extender bit_extender_2
  // Probe on negator_1_out
  Negator #(.width(4)) negator_1 (.in(bit_extender_1_out), .out(negator_1_out));
  Shifter #(.width(4), .shift("ar")) shifter_1 (.in(in_4), .\dist (2'b10), .out(shifter_1_out));
  // Probe on xnor_1_out
  assign out_7 = negator_1_out ^ shifter_1_out;  // Odd_Parity odd_parity_1, 4 bits wide
endmodule
