// Logisim project navigation.circ as structural Verilog
module fsm (
  input  [1:0] in_1,
  input  in_2,
  input  in_3,
  output out_4,
  output out_5
);

  wire [2:0] register_1_q;
  wire [3:0] \状态转移_1_a_2 ;

  \状态转移  \u_状态转移_1  (
    .A(register_1_q[2]), .B(register_1_q[1]), .C(register_1_q[0]), .D(in_1[1]), .E(in_1[0]),
    .A_2(\状态转移_1_a_2 [0]), .B_2(\状态转移_1_a_2 [1]), .C_2(\状态转移_1_a_2 [2]), .D_2(\状态转移_1_a_2 [3]));
  // Probe on \状态转移_1_a_2 
  Register #(.width(4)) register_1 (.D(\状态转移_1_a_2 ), .Q({out_5, register_1_q}), .clk(in_2), .clr(in_3));  // open: en
  Multiplexer #(.select(3)) multiplexer_1 (
    .in0(1'b0), .in1(1'b0), .in2(1'b0), .in3(1'b0), .in4(1'b1), .out(out_4), .sel(register_1_q));  // open: in5, in6, in7, en

  // Other names for the same wires on the sheet: clk = in_2; dir0 = in_1[0]; dir1 = in_1[1]; reset = in_3
endmodule

module \状态转移  (
  input  A,
  input  B,
  input  C,
  input  D,
  input  E,
  output A_2,
  output B_2,
  output C_2,
  output D_2
);

  wire and_1_out, and_2_out, and_3_out, and_4_out, and_5_out, and_6_out, and_7_out, and_8_out, and_9_out,
       and_10_out, and_11_out, and_12_out, and_13_out, and_14_out, and_15_out, and_16_out, and_17_out,
       and_18_out, and_19_out, and_20_out, and_21_out, and_22_out, and_23_out, and_24_out, and_25_out,
       and_26_out, and_27_out, and_28_out, and_29_out, and_30_out, and_31_out, and_32_out, and_33_out,
       and_34_out, and_35_out, and_36_out, and_37_out, and_38_out, and_39_out, and_40_out, and_41_out,
       and_42_out, not_1_out, not_2_out, not_3_out, not_4_out, not_5_out, not_6_out, not_7_out, not_8_out,
       not_9_out, not_10_out, not_11_out, not_12_out, not_13_out, not_14_out, not_15_out, not_16_out,
       not_17_out, not_18_out, not_19_out, not_20_out, not_21_out, not_22_out, not_23_out, not_24_out,
       not_25_out, not_26_out, not_27_out, not_28_out, or_2_out, or_3_out, or_4_out, or_5_out, or_6_out,
       or_7_out, or_9_out, or_10_out;

  not not_1 (not_1_out, C);
  not not_2 (not_2_out, D);
  not not_3 (not_3_out, E);
  not not_4 (not_4_out, D);
  not not_5 (not_5_out, B);
  not not_6 (not_6_out, D);
  not not_7 (not_7_out, A);
  not not_8 (not_8_out, B);
  not not_9 (not_9_out, D);
  not not_10 (not_10_out, E);
  not not_11 (not_11_out, A);
  not not_12 (not_12_out, C);
  not not_13 (not_13_out, D);
  not not_14 (not_14_out, A);
  not not_15 (not_15_out, B);
  not not_16 (not_16_out, C);
  and and_1 (and_1_out, B, not_1_out);
  and and_2 (and_2_out, not_2_out, not_3_out);
  and and_3 (and_3_out, B, C);
  and and_4 (and_4_out, not_4_out, E);
  and and_5 (and_5_out, not_5_out, C);
  not not_17 (not_17_out, D);
  and and_6 (and_6_out, C, not_6_out);
  not not_18 (not_18_out, E);
  not not_19 (not_19_out, C);
  not not_20 (not_20_out, D);
  not not_21 (not_21_out, C);
  not not_22 (not_22_out, E);
  and and_7 (and_7_out, not_7_out, not_8_out);
  and and_8 (and_8_out, not_9_out, not_10_out);
  and and_9 (and_9_out, C, D);
  and and_10 (and_10_out, B, D);
  and and_11 (and_11_out, B, C);
  not not_23 (not_23_out, E);
  and and_12 (and_12_out, not_11_out, not_12_out);
  and and_13 (and_13_out, not_13_out, E);
  and and_14 (and_14_out, not_14_out, not_15_out);
  and and_15 (and_15_out, not_16_out, D);
  not not_24 (not_24_out, A);
  not not_25 (not_25_out, C);
  not not_26 (not_26_out, E);
  not not_27 (not_27_out, D);
  not not_28 (not_28_out, E);
  and and_16 (and_16_out, and_1_out, and_2_out);
  or or_1 (A_2, and_16_out, and_17_out);
  and and_17 (and_17_out, and_3_out, and_4_out);
  and and_18 (and_18_out, and_5_out, not_17_out);
  or or_2 (or_2_out, and_18_out, and_19_out);
  and and_19 (and_19_out, and_6_out, not_18_out);
  and and_20 (and_20_out, B, not_19_out);
  and and_21 (and_21_out, and_20_out, and_22_out);
  and and_22 (and_22_out, not_20_out, E);
  and and_23 (and_23_out, B, not_21_out);
  and and_24 (and_24_out, and_23_out, and_25_out);
  and and_25 (and_25_out, D, not_22_out);
  and and_26 (and_26_out, B, C);
  and and_27 (and_27_out, and_26_out, and_28_out);
  and and_28 (and_28_out, D, E);
  and and_29 (and_29_out, and_7_out, and_8_out);
  or or_3 (or_3_out, and_29_out, and_30_out);
  and and_30 (and_30_out, and_9_out, E);
  and and_31 (and_31_out, and_10_out, E);
  or or_4 (or_4_out, and_31_out, and_32_out);
  and and_32 (and_32_out, and_11_out, not_23_out);
  and and_33 (and_33_out, and_12_out, and_13_out);
  or or_5 (or_5_out, and_33_out, and_34_out);
  and and_34 (and_34_out, and_14_out, and_15_out);
  and and_35 (and_35_out, not_24_out, not_25_out);
  and and_36 (and_36_out, and_35_out, and_37_out);
  and and_37 (and_37_out, D, not_26_out);
  and and_38 (and_38_out, C, D);
  and and_39 (and_39_out, and_38_out, E);
  and and_40 (and_40_out, B, C);
  and and_41 (and_41_out, and_40_out, and_42_out);
  and and_42 (and_42_out, not_27_out, not_28_out);
  or or_6 (or_6_out, or_2_out, and_21_out);
  or or_7 (or_7_out, and_24_out, and_27_out);
  or or_8 (C_2, or_3_out, or_4_out);
  or or_9 (or_9_out, or_5_out, and_36_out);
  or or_10 (or_10_out, and_39_out, and_41_out);
  or or_11 (B_2, or_6_out, or_7_out);
  or or_12 (D_2, or_9_out, or_10_out);
endmodule

module navigation (
  input  [1:0] in_1,
  input  in_2,
  input  in_3,
  output out_4,
  output out_5
);

  wire [2:0] register_1_q;
  wire [3:0] \状态转移_1_d_2 ;

  \状态转移  \u_状态转移_1  (
    .A(register_1_q[2]), .B(register_1_q[1]), .C(register_1_q[0]), .D(in_1[1]), .E(in_1[0]),
    .A_2(\状态转移_1_d_2 [3]), .B_2(\状态转移_1_d_2 [2]), .C_2(\状态转移_1_d_2 [1]), .D_2(\状态转移_1_d_2 [0]));
  // Probe on \状态转移_1_d_2 
  Register #(.width(4)) register_1 (.D(\状态转移_1_d_2 ), .Q({register_1_q, out_5}), .clk(in_2), .clr(in_3));  // open: en
  // Probe on register_1_q
  Multiplexer #(.select(3)) multiplexer_1 (
    .in0(1'b0), .in1(1'b0), .in2(1'b0), .in3(1'b0), .in4(1'b1), .in6(out_5), .out(out_4), .sel(register_1_q));  // open: in5, in7, en

  // Other names for the same wires on the sheet: clk = in_2; dir0 = in_1[0]; dir1 = in_1[1]; reset = in_3
endmodule
