// Logisim project swap.circ as structural Verilog
module main (
  input  [7:0] in_1,
  input  [7:0] in_2,
  output [3:0] out_3,
  output out_4
);

  wire bitfinder_1_found, bitselector_1_out;
  wire [2:0] bitfinder_1_index;
  wire [3:0] adder_1_out, bit_extender_1_out, bit_extender_2_out, bitadder_1_out;

  Shifter shifter_1 ();  // open: in, dist, out
  BitFinder #(.\type ("high1")) bitfinder_1 (.in(in_1), .index(bitfinder_1_index), .found(bitfinder_1_found));
  assign bit_extender_1_out = {{1{1'b0}}, bitfinder_1_index};  // Bit_Extender bit_extender_1
  assign bit_extender_2_out = {{3{1'b0}}, bitfinder_1_found};  // Bit_Extender bit_extender_2
  BitAdder bitadder_1 (.in0(in_2), .out(bitadder_1_out));
  BitSelector #(.width(4)) bitselector_1 (.in(bitadder_1_out), .out(bitselector_1_out), .sel(2'b00));
  Adder #(.width(4)) adder_1 (.a(bit_extender_1_out), .b(bit_extender_2_out), .out(adder_1_out));  // open: cin, cout
  Comparator #(.width(1)) comparator_1 (.a(bitselector_1_out), .b(1'b1), .eq(out_4));  // open: gt, lt
  Subtractor #(.width(4)) subtractor_1 (.a(4'b1000), .b(adder_1_out), .out(out_3));  // open: bin, bout
endmodule

module swap (
  input  a,
  input  b,
  input  c,
  output p,
  output q
);

  wire and_1_out, and_2_out, and_3_out, and_4_out, not_1_out, not_2_out;

  not not_1 (not_1_out, c);
  not not_2 (not_2_out, c);
  and and_1 (and_1_out, b, c);
  and and_2 (and_2_out, a, not_1_out);
  and and_3 (and_3_out, b, not_2_out);
  and and_4 (and_4_out, a, c);
  or or_1 (p, and_1_out, and_2_out);
  or or_2 (q, and_3_out, and_4_out);
endmodule

module swap1 (
  input  a,
  input  b,
  input  c,
  output p,
  output q
);

  wire and_1_out, and_2_out, and_3_out, and_4_out, not_1_out, not_2_out;

  not not_1 (not_1_out, c);
  not not_2 (not_2_out, c);
  and and_1 (and_1_out, b, c);
  and and_2 (and_2_out, a, not_1_out);
  and and_3 (and_3_out, b, not_2_out);
  and and_4 (and_4_out, a, c);
  or or_1 (p, and_1_out, and_2_out);
  or or_2 (q, and_3_out, and_4_out);
endmodule

module _1bit_swap (
  input  a,
  input  b,
  input  c,
  output p,
  output q
);

  wire and_1_out, and_2_out, and_3_out, and_4_out, not_1_out, not_2_out;

  not not_1 (not_1_out, c);
  not not_2 (not_2_out, c);
  and and_1 (and_1_out, b, c);
  and and_2 (and_2_out, a, not_1_out);
  and and_3 (and_3_out, b, not_2_out);
  and and_4 (and_4_out, a, c);
  or or_1 (p, and_1_out, and_2_out);
  or or_2 (q, and_3_out, and_4_out);
endmodule

module _4bit_swap (
  input  [3:0] in_1,
  input  [3:0] in_2,
  input  in_3,
  output [3:0] out_4,
  output [3:0] out_5
);

  _1bit_swap u_1bit_swap_1 (.a(in_1[0]), .b(in_2[0]), .c(in_3), .p(out_4[0]), .q(out_5[0]));
  _1bit_swap u_1bit_swap_2 (.a(in_1[1]), .b(in_2[1]), .c(in_3), .p(out_4[1]), .q(out_5[1]));
  _1bit_swap u_1bit_swap_3 (.a(in_1[2]), .b(in_2[2]), .c(in_3), .p(out_4[2]), .q(out_5[2]));
  _1bit_swap u_1bit_swap_4 (.a(in_1[3]), .b(in_2[3]), .c(in_3), .p(out_4[3]), .q(out_5[3]));
endmodule

module _4bit_sort (
  input  [3:0] in_1,
  input  [3:0] in_2,
  input  [3:0] in_3,
  input  [3:0] in_4,
  output [3:0] out_5,
  output [3:0] out_6,
  output [3:0] out_7,
  output [3:0] out_8
);

  wire comparator_1_gt, comparator_2_gt, comparator_3_gt, comparator_4_gt, comparator_5_gt, comparator_6_gt;
  wire [3:0] n4bit_swap_1_out_4, n4bit_swap_1_out_5, n4bit_swap_2_out_4, n4bit_swap_2_out_5,
       n4bit_swap_3_out_4, n4bit_swap_4_out_4, n4bit_swap_4_out_5, n4bit_swap_5_out_4;

  Comparator #(.width(4), .mode("unsigned")) comparator_1 (.a(in_1), .b(in_2), .gt(comparator_1_gt));  // open: eq, lt
  // Probe on n4bit_swap_1_out_5
  _4bit_swap u_4bit_swap_1 (
    .in_1(in_1), .in_2(in_2), .in_3(comparator_1_gt), .out_4(n4bit_swap_1_out_4), .out_5(n4bit_swap_1_out_5));
  // Probe on n4bit_swap_1_out_4
  Comparator #(.width(4), .mode("unsigned")) comparator_2 (
    .a(n4bit_swap_1_out_5), .b(in_3), .gt(comparator_2_gt));  // open: eq, lt
  // Probe on n4bit_swap_2_out_5
  // Probe on n4bit_swap_2_out_4
  _4bit_swap u_4bit_swap_2 (
    .in_1(n4bit_swap_1_out_5), .in_2(in_3), .in_3(comparator_2_gt), .out_4(n4bit_swap_2_out_4),
    .out_5(n4bit_swap_2_out_5));
  // Probe on n4bit_swap_2_out_5
  Comparator #(.width(4), .mode("unsigned")) comparator_3 (
    .a(n4bit_swap_2_out_5), .b(in_4), .gt(comparator_3_gt));  // open: eq, lt
  // Probe on n4bit_swap_3_out_4
  _4bit_swap u_4bit_swap_3 (
    .in_1(n4bit_swap_2_out_5), .in_2(in_4), .in_3(comparator_3_gt), .out_4(n4bit_swap_3_out_4), .out_5(out_8));
  // Probe on out_8
  Comparator #(.width(4), .mode("unsigned")) comparator_4 (
    .a(n4bit_swap_1_out_4), .b(n4bit_swap_2_out_4), .gt(comparator_4_gt));  // open: eq, lt
  _4bit_swap u_4bit_swap_4 (
    .in_1(n4bit_swap_1_out_4), .in_2(n4bit_swap_2_out_4), .in_3(comparator_4_gt), .out_4(n4bit_swap_4_out_4),
    .out_5(n4bit_swap_4_out_5));
  Comparator #(.width(4), .mode("unsigned")) comparator_5 (
    .a(n4bit_swap_4_out_5), .b(n4bit_swap_3_out_4), .gt(comparator_5_gt));  // open: eq, lt
  _4bit_swap u_4bit_swap_5 (
    .in_1(n4bit_swap_4_out_5), .in_2(n4bit_swap_3_out_4), .in_3(comparator_5_gt), .out_4(n4bit_swap_5_out_4),
    .out_5(out_7));
  Comparator #(.width(4), .mode("unsigned")) comparator_6 (
    .a(n4bit_swap_4_out_4), .b(n4bit_swap_5_out_4), .gt(comparator_6_gt));  // open: eq, lt
  _4bit_swap u_4bit_swap_6 (
    .in_1(n4bit_swap_4_out_4), .in_2(n4bit_swap_5_out_4), .in_3(comparator_6_gt), .out_4(out_5), .out_5(out_6));
endmodule
