// Logisim project 元器件搭建.circ as structural Verilog
module main (
  input  R,
  input  S,
  output out_3,
  output out_4
);

  wire or_1_out, or_2_out;

  or or_1 (or_1_out, R, out_4);
  or or_2 (or_2_out, out_3, S);
  not not_1 (out_3, or_1_out);
  not not_2 (out_4, or_2_out);
endmodule
