// Logisim project 时序电路计算斐波那契数列.circ as structural Verilog: 3 circuits, main circuit main
module main (
  input  [2:0] in_1,
  output [3:0] out_2
);

  wire output_signal;
  wire [3:0] fib_now;

  // Probe on output_signal
  \计数逻辑  \u_计数逻辑_1  (.in_1(in_1), .in_2(1'b0), .out_3(output_signal));
  \计算逻辑  \u_计算逻辑_1  (.in_1(1'b0), .freeze(output_signal), .out_3(fib_now));
  // Probe on fib_now
  Multiplexer #(.width(4)) multiplexer_1 (.in0(4'b0000), .in1(fib_now), .out(out_2), .sel(output_signal));  // open: en

  // Notes on the sheet:
  //   计数逻辑
  //   计算逻辑
endmodule

module \计算逻辑  (
  input  in_1,
  input  freeze,
  output [3:0] out_3
);

  wire clock_1_out, clock_2_out, clock_3_out, enable, initialize;
  wire [3:0] adder_1_out, multiplexer_1_out, prev;

  Counter #(.width(1), .max('h1), .ongoal("stay")) counter_1 (
    .Q(initialize), .clk(clock_1_out), .clr(in_1));  // open: load, D, count, carry
  Clock clock_1 (.out(clock_1_out));
  not not_1 (enable, freeze);
  Multiplexer #(.width(4)) multiplexer_1 (
    .in0(4'b0001), .in1(out_3), .out(multiplexer_1_out), .sel(initialize));  // open: en
  Clock clock_2 (.out(clock_2_out));
  Adder #(.width(4)) adder_1 (.a(out_3), .b(prev), .out(adder_1_out));  // open: cin, cout
  Register #(.width(4)) register_1 (.D(multiplexer_1_out), .en(enable), .Q(prev), .clk(clock_2_out), .clr(in_1));
  Register #(.width(4)) register_2 (.D(adder_1_out), .en(enable), .Q(out_3), .clk(clock_3_out), .clr(in_1));
  Clock clock_3 (.out(clock_3_out));

  // Other names for the same wires on the sheet: now[3:0] = out_3; reset = in_1

  // Notes on the sheet:
  //   prev
endmodule

module \计数逻辑  (
  input  [2:0] in_1,
  input  in_2,
  output out_3
);

  wire clock_1_out;
  wire [4:0] counter_value, max_value;

  assign max_value = {{2{1'b0}}, in_1};  // Bit_Extender bit_extender_1
  Counter #(.width(5), .max('h8), .ongoal("stay")) counter_1 (
    .Q(counter_value), .clk(clock_1_out), .clr(in_2));  // open: load, D, count, carry
  Clock clock_1 (.out(clock_1_out));
  Comparator #(.width(5)) comparator_1 (.a(max_value), .b(counter_value), .lt(out_3));  // open: gt, eq

  // Other names for the same wires on the sheet: reset = in_2
endmodule
