// Logisim project 状态机.circ as structural Verilog: 3 circuits, main circuit main
module main (
  output out_1
);

  wire clock_1_out;
  wire [2:0] counter_1_q;

  Clock clock_1 (.out(clock_1_out));
  Counter #(.width(1), .max('h1)) counter_1 (
    .Q(counter_1_q[0]), .carry(out_1), .clk(clock_1_out));  // open: load, D, count, clr
  ROM #(.addrWidth(3), .dataWidth(1)) rom_1 (.addr(counter_1_q));  // open: data, sel
  // Pins of 1 and 3 bits meet at counter_1_q
endmodule

module MOD5 (
  input  A,
  input  B,
  input  C,
  input  D,
  output A2,
  output B2,
  output C2
);

  wire and_1_out, and_2_out, and_3_out, and_4_out, and_5_out, and_6_out, and_7_out, and_8_out, and_9_out,
       and_10_out, not_1_out, not_2_out, not_3_out, not_4_out, not_5_out, not_6_out, not_7_out, not_8_out,
       not_9_out, not_10_out;

  not not_1 (not_1_out, A);
  and and_1 (and_1_out, not_1_out, B, not_2_out);
  not not_2 (not_2_out, D);
  and and_2 (and_2_out, A, C, D);
  and and_3 (and_3_out, A, B, not_3_out);
  not not_3 (not_3_out, C);
  not not_4 (not_4_out, A);
  and and_4 (and_4_out, not_4_out, D);
  not not_5 (not_5_out, B);
  and and_5 (and_5_out, not_5_out, D);
  and and_6 (and_6_out, A, C);
  and and_7 (and_7_out, A, B, not_6_out);
  not not_6 (not_6_out, D);
  not not_7 (not_7_out, B);
  and and_8 (and_8_out, not_7_out, not_8_out);
  not not_8 (not_8_out, D);
  not not_9 (not_9_out, A);
  and and_9 (and_9_out, not_9_out, B, D);
  and and_10 (and_10_out, A, not_10_out);
  not not_10 (not_10_out, D);
  or or_1 (A2, and_1_out, and_2_out, and_3_out);
  or or_2 (B2, and_4_out, and_5_out, and_6_out, and_7_out);
  or or_3 (C2, and_8_out, and_9_out, and_10_out);
endmodule

module mod5 (
  input  in_1,
  output out_2,
  output out_3,
  output out_4,
  output out_5,
  output out_6
);

  wire clock_1_out;
  wire [2:0] mod5_1_c2, state;

  MOD5 mod5_1 (
    .A(state[2]), .B(state[1]), .C(state[0]), .D(in_1), .A2(mod5_1_c2[2]), .B2(mod5_1_c2[1]),
    .C2(mod5_1_c2[0]));
  // Probe on mod5_1_c2
  Register #(.width(3)) register_1 (.D(mod5_1_c2), .Q(state), .clk(clock_1_out));  // open: en, clr
  Clock clock_1 (.out(clock_1_out));
  // Probe on mod5_1_c2
  // Probe on {out_6, out_5, out_4, out_3, out_2}
  Multiplexer #(.select(3), .width(5), .enable("false")) multiplexer_1 (
    .in0(5'b00010), .in1(5'b00010), .in2(5'b00100), .in3(5'b01000), .in4(5'b10000),
    .out({out_6, out_5, out_4, out_3, out_2}), .sel(mod5_1_c2));  // open: in5, in6, in7
endmodule
